// Logisim project Marina.circ as structural Verilog: 11 circuits, main circuit MARINA_8BITS_COMPUTER
module MARINA_8BITS_COMPUTER (
  input  PROGRAM_MODE,
  input  MANUAL_PROGRAMING,
  input  in_3,
  input  in_4,
  input  in_5,
  input  in_6,
  input  in_7,
  input  BUS_IN,
  input  in_9,
  input  INSTRUC,
  input  in_11,
  input  in_12,
  input  in_13,
  input  ADDR,
  input  in_15,
  input  in_16,
  input  in_17,
  input  in_18,
  input  in_19,
  input  in_20,
  input  in_21,
  input  in_22,
  input  in_23,
  input  in_24,
  input  in_25,
  input  in_26,
  input  in_27,
  input  in_28,
  output out_29,
  output out_30
);

  wire a_register_1_l0, a_register_1_l1, a_register_1_l2, a_register_1_l3, a_register_1_l4, a_register_1_l5,
       a_register_1_l6, a_register_1_l7, AI, alu_1_cf, alu_1_l0, alu_1_l1, alu_1_l2, alu_1_l3, alu_1_l4,
       alu_1_l5, alu_1_l6, alu_1_l7, alu_1_zf, AO, B_CLK, b_register_1_l0, b_register_1_l1, b_register_1_l2,
       b_register_1_l3, b_register_1_l4, b_register_1_l5, b_register_1_l6, b_register_1_l7, b_register_2_l0,
       b_register_2_l1, b_register_2_l2, b_register_2_l3, b_register_2_l4, b_register_2_l5, b_register_2_l6,
       b_register_2_l7, BI, BO, CE, CLK, clock_1_out, CO, decoder_8bits_to_7_segments_display_1_a0,
       decoder_8bits_to_7_segments_display_1_a1, decoder_8bits_to_7_segments_display_1_a2,
       decoder_8bits_to_7_segments_display_1_b0, decoder_8bits_to_7_segments_display_1_b1,
       decoder_8bits_to_7_segments_display_1_b2, decoder_8bits_to_7_segments_display_1_c0,
       decoder_8bits_to_7_segments_display_1_c1, decoder_8bits_to_7_segments_display_1_c2,
       decoder_8bits_to_7_segments_display_1_d0, decoder_8bits_to_7_segments_display_1_d1,
       decoder_8bits_to_7_segments_display_1_d2, decoder_8bits_to_7_segments_display_1_e0,
       decoder_8bits_to_7_segments_display_1_e1, decoder_8bits_to_7_segments_display_1_e2,
       decoder_8bits_to_7_segments_display_1_f0, decoder_8bits_to_7_segments_display_1_f1,
       decoder_8bits_to_7_segments_display_1_f2, decoder_8bits_to_7_segments_display_1_g0,
       decoder_8bits_to_7_segments_display_1_g1, decoder_8bits_to_7_segments_display_1_g2, EO, FI,
       flags_register_1_l0, flags_register_1_l1, HL, II, instrucion_register_1_l0, instrucion_register_1_l1,
       instrucion_register_1_l2, instrucion_register_1_l3, instrucion_register_1_l4,
       instrucion_register_1_l5, instrucion_register_1_l6, instrucion_register_1_l7,
       instruction_decoder_1_s0, instruction_decoder_1_s1, instruction_decoder_1_s2,
       instruction_decoder_1_s3, instruction_decoder_1_s4, instruction_decoder_1_s5,
       instruction_decoder_1_s6, instruction_decoder_1_s7, IO, JP, mar_1_l0, mar_1_l1, mar_1_l2, mar_1_l3,
       mar_1_l4, mar_1_l5, mar_1_l6, mar_1_l7, mar_1_l8, mar_1_l9, mar_1_la, mar_1_lb, mar_1_lc, mar_1_ld,
       mar_1_le, mar_1_lf, MI, OI, or_1_out, or_2_out, program_counter_1_l0, program_counter_1_l1,
       program_counter_1_l2, program_counter_1_l3, program_counter_1_l4, program_counter_1_l5,
       program_counter_1_l6, program_counter_1_l7, REST, RI, RO, SU;
  wire [7:0] instrucion_register_1_o0, ram_1_dout;
  wire [15:0] mar_1_addrs;

  RAM #(.addrWidth(16), .\type ("nonvolatile")) ram_1 (
    .addr(mar_1_addrs), .we(RI), .oe(RO), .clk(or_1_out), .din(instrucion_register_1_o0), .dout(ram_1_dout));
  or or_1 (or_1_out, RO, CLK);
  Clock clock_1 (.out(clock_1_out));
  MAR mar_1 (
    .ENABLE(1'b1), .I0(instrucion_register_1_o0[0]), .I1(instrucion_register_1_o0[1]),
    .I2(instrucion_register_1_o0[2]), .I3(instrucion_register_1_o0[3]), .CLOCK(CLK), .LOAD(MI), .RESET(REST),
    .L0(mar_1_l0), .L1(mar_1_l1), .L2(mar_1_l2), .L3(mar_1_l3), .L4(mar_1_l4), .L5(mar_1_l5), .L6(mar_1_l6),
    .L7(mar_1_l7), .L8(mar_1_l8), .L9(mar_1_l9), .LA(mar_1_la), .LB(mar_1_lb), .LC(mar_1_lc), .LD(mar_1_ld),
    .LE(mar_1_le), .LF(mar_1_lf), .ADDRS(mar_1_addrs));  // open: I4, I5, I6, I7
  DotMatrix #(.matrixcols(16), .matrixrows(1)) dotmatrix_1 (
    .col0(mar_1_l0), .col1(mar_1_l1), .col2(mar_1_l2), .col3(mar_1_l3), .col4(mar_1_l4), .col5(mar_1_l5),
    .col6(mar_1_l6), .col7(mar_1_l7), .col8(mar_1_l8), .col9(mar_1_l9), .col10(mar_1_la), .col11(mar_1_lb),
    .col12(mar_1_lc), .col13(mar_1_ld), .col14(mar_1_le), .col15(mar_1_lf));
  DotMatrix #(.matrixcols(4), .matrixrows(1)) dotmatrix_2 (
    .col0(instrucion_register_1_l7), .col1(instrucion_register_1_l6), .col2(instrucion_register_1_l5),
    .col3(instrucion_register_1_l4));
  DotMatrix #(.matrixcols(4), .matrixrows(1)) dotmatrix_3 (
    .col0(instrucion_register_1_l3), .col1(instrucion_register_1_l2), .col2(instrucion_register_1_l1),
    .col3(instrucion_register_1_l0));
  INSTRUCTION_DECODER instruction_decoder_1 (
    .PROGRAM_MODE(PROGRAM_MODE), .ZF(out_30), .CF(out_29), .OP0(instrucion_register_1_l4),
    .OP1(instrucion_register_1_l5), .OP2(instrucion_register_1_l6), .OP3(instrucion_register_1_l7),
    .COLCK(CLK), .CLEAR(REST), .HL(HL), .OI(OI), .IO(IO), .II(II), .RO(RO), .RI(RI), .MI(MI), .FI(FI),
    .BO(BO), .BI(BI), .SU(SU), .EO(EO), .AO(AO), .AI(AI), .JP(JP), .CO(CO), .CE(CE),
    .S0(instruction_decoder_1_s0), .S1(instruction_decoder_1_s1), .S2(instruction_decoder_1_s2),
    .S3(instruction_decoder_1_s3), .S4(instruction_decoder_1_s4), .S5(instruction_decoder_1_s5),
    .S6(instruction_decoder_1_s6), .S7(instruction_decoder_1_s7));
  or or_2 (or_2_out, clock_1_out, B_CLK);
  INSTRUCION_REGISTER instrucion_register_1 (
    .ENABLE(IO), .I0(instrucion_register_1_o0[0]), .I1(instrucion_register_1_o0[1]),
    .I2(instrucion_register_1_o0[2]), .I3(instrucion_register_1_o0[3]), .I4(instrucion_register_1_o0[4]),
    .I5(instrucion_register_1_o0[5]), .I6(instrucion_register_1_o0[6]), .I7(instrucion_register_1_o0[7]),
    .CLOCK(CLK), .LOAD(II), .RESET(REST), .O0(instrucion_register_1_o0[0]), .O1(instrucion_register_1_o0[1]),
    .O2(instrucion_register_1_o0[2]), .O3(instrucion_register_1_o0[3]), .O4(instrucion_register_1_o0[4]),
    .O5(instrucion_register_1_o0[5]), .O6(instrucion_register_1_o0[6]), .O7(instrucion_register_1_o0[7]),
    .L0(instrucion_register_1_l0), .L1(instrucion_register_1_l1), .L2(instrucion_register_1_l2),
    .L3(instrucion_register_1_l3), .L4(instrucion_register_1_l4), .L5(instrucion_register_1_l5),
    .L6(instrucion_register_1_l6), .L7(instrucion_register_1_l7));
  DotMatrix #(.matrixcols(8), .matrixrows(1)) dotmatrix_4 (
    .col0(instruction_decoder_1_s0), .col1(instruction_decoder_1_s1), .col2(instruction_decoder_1_s2),
    .col3(instruction_decoder_1_s3), .col4(instruction_decoder_1_s4), .col5(instruction_decoder_1_s5),
    .col6(instruction_decoder_1_s6), .col7(instruction_decoder_1_s7));
  and and_1 (CLK, or_2_out, ~HL);  // AND_Gate
  DotMatrix #(.matrixcols(4), .matrixrows(1)) dotmatrix_5 (
    .col0(instrucion_register_1_o0[3]), .col1(instrucion_register_1_o0[2]),
    .col2(instrucion_register_1_o0[1]), .col3(instrucion_register_1_o0[0]));
  Button CLCK (.out(B_CLK));
  Button RESET (.out(REST));
  assign instrucion_register_1_o0[0] = BUS_IN ? in_17 : 1'bz;  // Controlled_Buffer controlled_buffer_1
  assign instrucion_register_1_o0[1] = BUS_IN ? in_16 : 1'bz;  // Controlled_Buffer controlled_buffer_2
  assign instrucion_register_1_o0[2] = BUS_IN ? in_15 : 1'bz;  // Controlled_Buffer controlled_buffer_3
  assign instrucion_register_1_o0[3] = BUS_IN ? ADDR : 1'bz;  // Controlled_Buffer controlled_buffer_4
  assign instrucion_register_1_o0[4] = BUS_IN ? in_13 : 1'bz;  // Controlled_Buffer controlled_buffer_5
  assign instrucion_register_1_o0[5] = BUS_IN ? in_12 : 1'bz;  // Controlled_Buffer controlled_buffer_6
  assign instrucion_register_1_o0[6] = BUS_IN ? in_11 : 1'bz;  // Controlled_Buffer controlled_buffer_7
  assign instrucion_register_1_o0[7] = BUS_IN ? INSTRUC : 1'bz;  // Controlled_Buffer controlled_buffer_8
  assign instrucion_register_1_o0[0] = RO ? ram_1_dout[0] : 1'bz;  // Controlled_Buffer controlled_buffer_9
  assign instrucion_register_1_o0[1] = RO ? ram_1_dout[1] : 1'bz;  // Controlled_Buffer controlled_buffer_10
  assign instrucion_register_1_o0[2] = RO ? ram_1_dout[2] : 1'bz;  // Controlled_Buffer controlled_buffer_11
  assign instrucion_register_1_o0[3] = RO ? ram_1_dout[3] : 1'bz;  // Controlled_Buffer controlled_buffer_12
  assign instrucion_register_1_o0[4] = RO ? ram_1_dout[4] : 1'bz;  // Controlled_Buffer controlled_buffer_13
  assign instrucion_register_1_o0[5] = RO ? ram_1_dout[5] : 1'bz;  // Controlled_Buffer controlled_buffer_14
  assign instrucion_register_1_o0[6] = RO ? ram_1_dout[6] : 1'bz;  // Controlled_Buffer controlled_buffer_15
  assign instrucion_register_1_o0[7] = RO ? ram_1_dout[7] : 1'bz;  // Controlled_Buffer controlled_buffer_16
  DotMatrix #(.matrixcols(8), .matrixrows(1)) dotmatrix_6 (
    .col0(instrucion_register_1_o0[7]), .col1(instrucion_register_1_o0[6]),
    .col2(instrucion_register_1_o0[5]), .col3(instrucion_register_1_o0[4]),
    .col4(instrucion_register_1_o0[3]), .col5(instrucion_register_1_o0[2]),
    .col6(instrucion_register_1_o0[1]), .col7(instrucion_register_1_o0[0]));
  DotMatrix #(.matrixcols(8), .matrixrows(1)) dotmatrix_7 (
    .col0(instrucion_register_1_o0[7]), .col1(instrucion_register_1_o0[6]),
    .col2(instrucion_register_1_o0[5]), .col3(instrucion_register_1_o0[4]),
    .col4(instrucion_register_1_o0[3]), .col5(instrucion_register_1_o0[2]),
    .col6(instrucion_register_1_o0[1]), .col7(instrucion_register_1_o0[0]));
  _7_Segment_Display #(.decimalPoint("false")) u_7_segment_display_1 (
    .g(decoder_8bits_to_7_segments_display_1_g1), .f(decoder_8bits_to_7_segments_display_1_f1),
    .a(decoder_8bits_to_7_segments_display_1_a1), .b(decoder_8bits_to_7_segments_display_1_b1),
    .e(decoder_8bits_to_7_segments_display_1_e1), .d(decoder_8bits_to_7_segments_display_1_d1),
    .c(decoder_8bits_to_7_segments_display_1_c1));
  _7_Segment_Display #(.decimalPoint("false")) u_7_segment_display_2 (
    .g(decoder_8bits_to_7_segments_display_1_g0), .f(decoder_8bits_to_7_segments_display_1_f0),
    .a(decoder_8bits_to_7_segments_display_1_a0), .b(decoder_8bits_to_7_segments_display_1_b0),
    .e(decoder_8bits_to_7_segments_display_1_e0), .d(decoder_8bits_to_7_segments_display_1_d0),
    .c(decoder_8bits_to_7_segments_display_1_c0));
  DECODER_8BITS_TO_7_SEGMENTS_DISPLAY decoder_8bits_to_7_segments_display_1 (
    .I0(b_register_1_l0), .I1(b_register_1_l1), .I2(b_register_1_l2), .I3(b_register_1_l3),
    .I4(b_register_1_l4), .I5(b_register_1_l5), .I6(b_register_1_l6), .I7(b_register_1_l7),
    .A0(decoder_8bits_to_7_segments_display_1_a0), .B0(decoder_8bits_to_7_segments_display_1_b0),
    .C0(decoder_8bits_to_7_segments_display_1_c0), .D0(decoder_8bits_to_7_segments_display_1_d0),
    .E0(decoder_8bits_to_7_segments_display_1_e0), .F0(decoder_8bits_to_7_segments_display_1_f0),
    .G0(decoder_8bits_to_7_segments_display_1_g0), .A1(decoder_8bits_to_7_segments_display_1_a1),
    .B1(decoder_8bits_to_7_segments_display_1_b1), .C1(decoder_8bits_to_7_segments_display_1_c1),
    .D1(decoder_8bits_to_7_segments_display_1_d1), .E1(decoder_8bits_to_7_segments_display_1_e1),
    .F1(decoder_8bits_to_7_segments_display_1_f1), .G1(decoder_8bits_to_7_segments_display_1_g1),
    .A2(decoder_8bits_to_7_segments_display_1_a2), .B2(decoder_8bits_to_7_segments_display_1_b2),
    .C2(decoder_8bits_to_7_segments_display_1_c2), .D2(decoder_8bits_to_7_segments_display_1_d2),
    .E2(decoder_8bits_to_7_segments_display_1_e2), .F2(decoder_8bits_to_7_segments_display_1_f2),
    .G2(decoder_8bits_to_7_segments_display_1_g2));
  DotMatrix #(.matrixcols(8), .matrixrows(1)) dotmatrix_8 (
    .col0(b_register_1_l7), .col1(b_register_1_l6), .col2(b_register_1_l5), .col3(b_register_1_l4),
    .col4(b_register_1_l3), .col5(b_register_1_l2), .col6(b_register_1_l1), .col7(b_register_1_l0));
  DotMatrix #(.matrixcols(8), .matrixrows(1)) dotmatrix_9 (
    .col0(a_register_1_l7), .col1(a_register_1_l6), .col2(a_register_1_l5), .col3(a_register_1_l4),
    .col4(a_register_1_l3), .col5(a_register_1_l2), .col6(a_register_1_l1), .col7(a_register_1_l0));
  DotMatrix #(.matrixcols(8), .matrixrows(1)) dotmatrix_10 (
    .col0(b_register_2_l7), .col1(b_register_2_l6), .col2(b_register_2_l5), .col3(b_register_2_l4),
    .col4(b_register_2_l3), .col5(b_register_2_l2), .col6(b_register_2_l1), .col7(b_register_2_l0));
  assign MI = MANUAL_PROGRAMING ? in_3 : 1'bz;  // Controlled_Buffer controlled_buffer_17
  assign RI = MANUAL_PROGRAMING ? in_6 : 1'bz;  // Controlled_Buffer controlled_buffer_18
  assign RO = MANUAL_PROGRAMING ? in_9 : 1'bz;  // Controlled_Buffer controlled_buffer_19
  assign II = MANUAL_PROGRAMING ? in_18 : 1'bz;  // Controlled_Buffer controlled_buffer_20
  assign IO = MANUAL_PROGRAMING ? in_19 : 1'bz;  // Controlled_Buffer controlled_buffer_21
  assign OI = MANUAL_PROGRAMING ? in_21 : 1'bz;  // Controlled_Buffer controlled_buffer_22
  assign BI = MANUAL_PROGRAMING ? in_23 : 1'bz;  // Controlled_Buffer controlled_buffer_23
  assign BO = MANUAL_PROGRAMING ? in_25 : 1'bz;  // Controlled_Buffer controlled_buffer_24
  _7_Segment_Display #(.decimalPoint("false")) u_7_segment_display_3 (
    .g(decoder_8bits_to_7_segments_display_1_g2), .f(decoder_8bits_to_7_segments_display_1_f2),
    .a(decoder_8bits_to_7_segments_display_1_a2), .b(decoder_8bits_to_7_segments_display_1_b2),
    .e(decoder_8bits_to_7_segments_display_1_e2), .d(decoder_8bits_to_7_segments_display_1_d2),
    .c(decoder_8bits_to_7_segments_display_1_c2));
  B_REGISTER b_register_1 (
    .I0(instrucion_register_1_o0[0]), .I1(instrucion_register_1_o0[1]), .I2(instrucion_register_1_o0[2]),
    .I3(instrucion_register_1_o0[3]), .I4(instrucion_register_1_o0[4]), .I5(instrucion_register_1_o0[5]),
    .I6(instrucion_register_1_o0[6]), .I7(instrucion_register_1_o0[7]), .CLOCK(CLK), .LOAD(OI), .RESET(REST),
    .L0(b_register_1_l0), .L1(b_register_1_l1), .L2(b_register_1_l2), .L3(b_register_1_l3),
    .L4(b_register_1_l4), .L5(b_register_1_l5), .L6(b_register_1_l6), .L7(b_register_1_l7));  // open: ENABLE, O0, O1, O2, O3, O4, O5, O6, O7
  PROGRAM_COUNTER program_counter_1 (
    .COut(CO), .CEnable(CE), .CWrite(JP), .CReset(REST), .CLOCK(CLK), .I3(instrucion_register_1_o0[3]),
    .I2(instrucion_register_1_o0[2]), .I1(instrucion_register_1_o0[1]), .I0(instrucion_register_1_o0[0]),
    .O3(instrucion_register_1_o0[3]), .O2(instrucion_register_1_o0[2]), .O1(instrucion_register_1_o0[1]),
    .O0(instrucion_register_1_o0[0]), .L7(program_counter_1_l7), .L6(program_counter_1_l6),
    .L5(program_counter_1_l5), .L4(program_counter_1_l4), .L3(program_counter_1_l3),
    .L2(program_counter_1_l2), .L1(program_counter_1_l1), .L0(program_counter_1_l0));  // open: I7, I6, I5, I4, O7, O6, O5, O4
  DotMatrix #(.matrixcols(8), .matrixrows(1)) dotmatrix_11 (
    .col0(program_counter_1_l0), .col1(program_counter_1_l1), .col2(program_counter_1_l2),
    .col3(program_counter_1_l3), .col4(program_counter_1_l4), .col5(program_counter_1_l5),
    .col6(program_counter_1_l6), .col7(program_counter_1_l7));
  A_REGISTER a_register_1 (
    .ENABLE(AO), .I0(instrucion_register_1_o0[0]), .I1(instrucion_register_1_o0[1]),
    .I2(instrucion_register_1_o0[2]), .I3(instrucion_register_1_o0[3]), .I4(instrucion_register_1_o0[4]),
    .I5(instrucion_register_1_o0[5]), .I6(instrucion_register_1_o0[6]), .I7(instrucion_register_1_o0[7]),
    .CLOCK(CLK), .LOAD(AI), .RESET(REST), .O0(instrucion_register_1_o0[0]), .O1(instrucion_register_1_o0[1]),
    .O2(instrucion_register_1_o0[2]), .O3(instrucion_register_1_o0[3]), .O4(instrucion_register_1_o0[4]),
    .O5(instrucion_register_1_o0[5]), .O6(instrucion_register_1_o0[6]), .O7(instrucion_register_1_o0[7]),
    .L0(a_register_1_l0), .L1(a_register_1_l1), .L2(a_register_1_l2), .L3(a_register_1_l3),
    .L4(a_register_1_l4), .L5(a_register_1_l5), .L6(a_register_1_l6), .L7(a_register_1_l7));
  B_REGISTER b_register_2 (
    .ENABLE(BO), .I0(instrucion_register_1_o0[0]), .I1(instrucion_register_1_o0[1]),
    .I2(instrucion_register_1_o0[2]), .I3(instrucion_register_1_o0[3]), .I4(instrucion_register_1_o0[4]),
    .I5(instrucion_register_1_o0[5]), .I6(instrucion_register_1_o0[6]), .I7(instrucion_register_1_o0[7]),
    .CLOCK(CLK), .LOAD(BI), .RESET(REST), .O0(instrucion_register_1_o0[0]), .O1(instrucion_register_1_o0[1]),
    .O2(instrucion_register_1_o0[2]), .O3(instrucion_register_1_o0[3]), .O4(instrucion_register_1_o0[4]),
    .O5(instrucion_register_1_o0[5]), .O6(instrucion_register_1_o0[6]), .O7(instrucion_register_1_o0[7]),
    .L0(b_register_2_l0), .L1(b_register_2_l1), .L2(b_register_2_l2), .L3(b_register_2_l3),
    .L4(b_register_2_l4), .L5(b_register_2_l5), .L6(b_register_2_l6), .L7(b_register_2_l7));
  assign CO = MANUAL_PROGRAMING ? in_4 : 1'bz;  // Controlled_Buffer controlled_buffer_25
  assign JP = MANUAL_PROGRAMING ? in_5 : 1'bz;  // Controlled_Buffer controlled_buffer_26
  assign CE = MANUAL_PROGRAMING ? in_7 : 1'bz;  // Controlled_Buffer controlled_buffer_27
  assign SU = MANUAL_PROGRAMING ? in_20 : 1'bz;  // Controlled_Buffer controlled_buffer_28
  assign EO = MANUAL_PROGRAMING ? in_22 : 1'bz;  // Controlled_Buffer controlled_buffer_29
  assign AI = MANUAL_PROGRAMING ? in_24 : 1'bz;  // Controlled_Buffer controlled_buffer_30
  assign AO = MANUAL_PROGRAMING ? in_26 : 1'bz;  // Controlled_Buffer controlled_buffer_31
  assign FI = MANUAL_PROGRAMING ? in_27 : 1'bz;  // Controlled_Buffer controlled_buffer_32
  assign HL = MANUAL_PROGRAMING ? in_28 : 1'bz;  // Controlled_Buffer controlled_buffer_33
  DotMatrix #(.matrixcols(8), .matrixrows(1)) dotmatrix_12 (
    .col0(alu_1_l7), .col1(alu_1_l6), .col2(alu_1_l5), .col3(alu_1_l4), .col4(alu_1_l3), .col5(alu_1_l2),
    .col6(alu_1_l1), .col7(alu_1_l0));
  ALU alu_1 (
    .ENABLE(EO), .A7(a_register_1_l7), .B7(b_register_2_l7), .A6(a_register_1_l6), .B6(b_register_2_l6),
    .A5(a_register_1_l5), .B5(b_register_2_l5), .A4(a_register_1_l4), .B4(b_register_2_l4),
    .A3(a_register_1_l3), .B3(b_register_2_l3), .A2(a_register_1_l2), .B2(b_register_2_l2),
    .A1(a_register_1_l1), .B1(b_register_2_l1), .A0(a_register_1_l0), .B0(b_register_2_l0), .su(SU),
    .E0(instrucion_register_1_o0[0]), .E1(instrucion_register_1_o0[1]), .E2(instrucion_register_1_o0[2]),
    .E3(instrucion_register_1_o0[3]), .E4(instrucion_register_1_o0[4]), .E5(instrucion_register_1_o0[5]),
    .E6(instrucion_register_1_o0[6]), .E7(instrucion_register_1_o0[7]), .CF(alu_1_cf), .ZF(alu_1_zf),
    .L7(alu_1_l7), .L6(alu_1_l6), .L5(alu_1_l5), .L4(alu_1_l4), .L3(alu_1_l3), .L2(alu_1_l2), .L1(alu_1_l1),
    .L0(alu_1_l0));
  FLAGS_REGISTER flags_register_1 (
    .I0(alu_1_cf), .I1(alu_1_zf), .CLOCK(CLK), .LOAD(FI), .RESET(REST), .ENABLE(1'b1),
    .L0(flags_register_1_l0), .L1(flags_register_1_l1), .O0(out_29), .O1(out_30));
  DotMatrix #(.matrixcols(2), .matrixrows(1)) dotmatrix_13 (.col0(flags_register_1_l0), .col1(flags_register_1_l1));

  // Other names for the same wires on the sheet: CF = out_29; ZF = out_30

  // Notes on the sheet:
  //   MARINA
  //   OUT-REGISTER
  //   A-REGISTER
  //   B-REGISTER
endmodule

module PROGRAM_COUNTER (
  input  COut,
  input  CEnable,
  input  CWrite,
  input  CReset,
  input  CLOCK,
  input  I7,
  input  I6,
  input  I5,
  input  I4,
  input  I3,
  input  I2,
  input  I1,
  input  I0,
  output O7,
  output O6,
  output O5,
  output O4,
  output O3,
  output O2,
  output O1,
  output O0,
  output L7,
  output L6,
  output L5,
  output L4,
  output L3,
  output L2,
  output L1,
  output L0
);

  wire and_1_out, and_2_out, and_3_out, and_4_out, and_5_out, and_6_out, and_7_out, and_8_out, and_9_out,
       and_10_out, and_11_out, and_12_out, and_13_out, and_14_out, and_15_out, and_16_out, j_k_ff_2_qn,
       j_k_ff_3_qn, j_k_ff_4_qn, j_k_ff_5_qn, j_k_ff_6_qn, j_k_ff_7_qn, j_k_ff_8_qn, or_1_out, or_2_out,
       or_3_out, or_4_out, or_5_out, or_6_out, or_7_out, or_8_out;

  J_K_Flip_Flop j_k_ff_1 (
    .J(CEnable), .K(CEnable), .clk(j_k_ff_2_qn), .Q(L7), .preset(and_1_out), .reset(or_1_out));  // open: Qn
  or or_1 (or_1_out, CReset, and_2_out);
  and and_1 (and_1_out, CWrite, I7, CLOCK);
  and and_2 (and_2_out, CWrite, ~I7, CLOCK);  // AND_Gate
  J_K_Flip_Flop j_k_ff_2 (
    .J(CEnable), .K(CEnable), .clk(j_k_ff_3_qn), .Q(L6), .Qn(j_k_ff_2_qn), .preset(and_3_out),
    .reset(or_2_out));
  or or_2 (or_2_out, CReset, and_4_out);
  and and_3 (and_3_out, CWrite, I6, CLOCK);
  and and_4 (and_4_out, CWrite, ~I6, CLOCK);  // AND_Gate
  assign O7 = COut ? L7 : 1'bz;  // Controlled_Buffer controlled_buffer_1
  assign O6 = COut ? L6 : 1'bz;  // Controlled_Buffer controlled_buffer_2
  J_K_Flip_Flop j_k_ff_3 (
    .J(CEnable), .K(CEnable), .clk(j_k_ff_4_qn), .Q(L5), .Qn(j_k_ff_3_qn), .preset(and_5_out),
    .reset(or_3_out));
  or or_3 (or_3_out, CReset, and_6_out);
  and and_5 (and_5_out, CWrite, I5, CLOCK);
  and and_6 (and_6_out, CWrite, ~I5, CLOCK);  // AND_Gate
  assign O5 = COut ? L5 : 1'bz;  // Controlled_Buffer controlled_buffer_3
  assign O4 = COut ? L4 : 1'bz;  // Controlled_Buffer controlled_buffer_4
  assign O3 = COut ? L3 : 1'bz;  // Controlled_Buffer controlled_buffer_5
  assign O2 = COut ? L2 : 1'bz;  // Controlled_Buffer controlled_buffer_6
  J_K_Flip_Flop j_k_ff_4 (
    .J(CEnable), .K(CEnable), .clk(j_k_ff_5_qn), .Q(L4), .Qn(j_k_ff_4_qn), .preset(and_7_out),
    .reset(or_4_out));
  or or_4 (or_4_out, CReset, and_8_out);
  and and_7 (and_7_out, CWrite, I4, CLOCK);
  and and_8 (and_8_out, CWrite, ~I4, CLOCK);  // AND_Gate
  assign O1 = COut ? L1 : 1'bz;  // Controlled_Buffer controlled_buffer_7
  assign O0 = COut ? L0 : 1'bz;  // Controlled_Buffer controlled_buffer_8
  J_K_Flip_Flop j_k_ff_5 (
    .J(CEnable), .K(CEnable), .clk(j_k_ff_6_qn), .Q(L3), .Qn(j_k_ff_5_qn), .preset(and_9_out),
    .reset(or_5_out));
  or or_5 (or_5_out, CReset, and_10_out);
  and and_9 (and_9_out, CWrite, I3, CLOCK);
  J_K_Flip_Flop j_k_ff_6 (
    .J(CEnable), .K(CEnable), .clk(j_k_ff_7_qn), .Q(L2), .Qn(j_k_ff_6_qn), .preset(and_11_out),
    .reset(or_6_out));
  and and_10 (and_10_out, CWrite, ~I3, CLOCK);  // AND_Gate
  and and_11 (and_11_out, CWrite, I2, CLOCK);
  J_K_Flip_Flop j_k_ff_7 (
    .J(CEnable), .K(CEnable), .clk(j_k_ff_8_qn), .Q(L1), .Qn(j_k_ff_7_qn), .preset(and_13_out),
    .reset(or_7_out));
  or or_6 (or_6_out, CReset, and_12_out);
  and and_12 (and_12_out, CWrite, ~I2, CLOCK);  // AND_Gate
  and and_13 (and_13_out, CWrite, I1, CLOCK);
  or or_7 (or_7_out, CReset, and_15_out);
  and and_14 (and_14_out, CWrite, I0, CLOCK);
  and and_15 (and_15_out, CWrite, ~I1, CLOCK);  // AND_Gate
  J_K_Flip_Flop j_k_ff_8 (
    .J(CEnable), .K(CEnable), .clk(CLOCK), .Q(L0), .Qn(j_k_ff_8_qn), .preset(and_14_out), .reset(or_8_out));
  or or_8 (or_8_out, CReset, and_16_out);
  and and_16 (and_16_out, CWrite, ~I0, CLOCK);  // AND_Gate
endmodule

module MAR (
  input  CLOCK,
  input  LOAD,
  input  RESET,
  input  ENABLE,
  input  I0,
  input  I1,
  input  I2,
  input  I3,
  input  I4,
  input  I5,
  input  I6,
  input  I7,
  output L0,
  output L1,
  output L2,
  output L3,
  output L4,
  output L5,
  output L6,
  output L7,
  output L8,
  output L9,
  output LA,
  output LB,
  output LC,
  output LD,
  output LE,
  output LF,
  output [15:0] ADDRS
);

  wire register_1_q, register_2_q, register_3_q, register_4_q, register_5_q, register_6_q, register_7_q,
       register_8_q;

  Register #(.width(1)) register_1 (.D(I0), .en(LOAD), .clk(CLOCK), .Q(register_1_q), .clr(RESET));
  Register #(.width(1)) register_2 (.D(I1), .en(LOAD), .clk(CLOCK), .Q(register_2_q), .clr(RESET));
  Register #(.width(1)) register_3 (.D(I2), .en(LOAD), .clk(CLOCK), .Q(register_3_q), .clr(RESET));
  Register #(.width(1)) register_4 (.D(I3), .en(LOAD), .clk(CLOCK), .Q(register_4_q), .clr(RESET));
  Register #(.width(1)) register_5 (.D(I4), .en(LOAD), .clk(CLOCK), .Q(register_5_q), .clr(RESET));
  Register #(.width(1)) register_6 (.D(I5), .en(LOAD), .clk(CLOCK), .Q(register_6_q), .clr(RESET));
  Register #(.width(1)) register_7 (.D(I6), .en(LOAD), .clk(CLOCK), .Q(register_7_q), .clr(RESET));
  Register #(.width(1)) register_8 (.D(I7), .en(LOAD), .clk(CLOCK), .Q(register_8_q), .clr(RESET));
  DECODER_4BITS decoder_4bits_1 (
    .I3(register_4_q), .I2(register_3_q), .I1(register_2_q), .I0(register_1_q), .ENABLE(1'b1), .DF(LF),
    .DE(LE), .DD(LD), .DC(LC), .DB(LB), .DA(LA), .D9(L9), .D8(L8), .D7(L7), .D6(L6), .D5(L5), .D4(L4),
    .D3(L3), .D2(L2), .D1(L1), .D0(L0));
  assign ADDRS[4] = ENABLE ? L4 : 1'bz;  // Controlled_Buffer controlled_buffer_1
  assign ADDRS[5] = ENABLE ? L5 : 1'bz;  // Controlled_Buffer controlled_buffer_2
  assign ADDRS[6] = ENABLE ? L6 : 1'bz;  // Controlled_Buffer controlled_buffer_3
  assign ADDRS[7] = ENABLE ? L7 : 1'bz;  // Controlled_Buffer controlled_buffer_4
  assign ADDRS[12] = ENABLE ? LC : 1'bz;  // Controlled_Buffer controlled_buffer_5
  assign ADDRS[13] = ENABLE ? LD : 1'bz;  // Controlled_Buffer controlled_buffer_6
  assign ADDRS[14] = ENABLE ? LE : 1'bz;  // Controlled_Buffer controlled_buffer_7
  assign ADDRS[15] = ENABLE ? LF : 1'bz;  // Controlled_Buffer controlled_buffer_8
  assign ADDRS[0] = ENABLE ? L0 : 1'bz;  // Controlled_Buffer controlled_buffer_9
  assign ADDRS[1] = ENABLE ? L1 : 1'bz;  // Controlled_Buffer controlled_buffer_10
  assign ADDRS[2] = ENABLE ? L2 : 1'bz;  // Controlled_Buffer controlled_buffer_11
  assign ADDRS[3] = ENABLE ? L3 : 1'bz;  // Controlled_Buffer controlled_buffer_12
  assign ADDRS[8] = ENABLE ? L8 : 1'bz;  // Controlled_Buffer controlled_buffer_13
  assign ADDRS[9] = ENABLE ? L9 : 1'bz;  // Controlled_Buffer controlled_buffer_14
  assign ADDRS[10] = ENABLE ? LA : 1'bz;  // Controlled_Buffer controlled_buffer_15
  assign ADDRS[11] = ENABLE ? LB : 1'bz;  // Controlled_Buffer controlled_buffer_16
endmodule

module DECODER_4BITS (
  input  ENABLE,
  input  I3,
  input  I2,
  input  I1,
  input  I0,
  output DF,
  output DE,
  output DD,
  output DC,
  output DB,
  output DA,
  output D9,
  output D8,
  output D7,
  output D6,
  output D5,
  output D4,
  output D3,
  output D2,
  output D1,
  output D0
);

  wire and_1_out, and_2_out, and_3_out, and_4_out, and_5_out, and_6_out, and_7_out, and_8_out, and_9_out,
       and_10_out, and_11_out, and_12_out, and_13_out, and_14_out, and_15_out, and_16_out, not_1_out,
       not_2_out, not_3_out, not_4_out;

  not not_1 (not_1_out, I3);
  not not_2 (not_2_out, I2);
  not not_3 (not_3_out, I1);
  not not_4 (not_4_out, I0);
  and and_1 (and_1_out, not_1_out, not_2_out, not_3_out, not_4_out);
  and and_2 (and_2_out, not_1_out, not_2_out, not_3_out, I0);
  and and_3 (and_3_out, not_1_out, not_2_out, I1, not_4_out);
  and and_4 (and_4_out, not_1_out, not_2_out, I1, I0);
  and and_5 (and_5_out, not_1_out, I2, not_3_out, not_4_out);
  and and_6 (and_6_out, not_1_out, I2, not_3_out, I0);
  and and_7 (and_7_out, not_1_out, I2, I1, not_4_out);
  and and_8 (and_8_out, not_1_out, I2, I1, I0);
  and and_9 (and_9_out, I3, not_2_out, not_3_out, not_4_out);
  and and_10 (and_10_out, I3, not_2_out, not_3_out, I0);
  and and_11 (and_11_out, I3, not_2_out, I1, not_4_out);
  and and_12 (and_12_out, I3, not_2_out, I1, I0);
  and and_13 (and_13_out, I3, I2, not_3_out, not_4_out);
  and and_14 (and_14_out, I3, I2, not_3_out, I0);
  and and_15 (and_15_out, I3, I2, I1, not_4_out);
  and and_16 (and_16_out, I3, I2, I1, I0);
  assign DF = ENABLE ? and_16_out : 1'bz;  // Controlled_Buffer controlled_buffer_1
  assign DE = ENABLE ? and_15_out : 1'bz;  // Controlled_Buffer controlled_buffer_2
  assign DD = ENABLE ? and_14_out : 1'bz;  // Controlled_Buffer controlled_buffer_3
  assign DC = ENABLE ? and_13_out : 1'bz;  // Controlled_Buffer controlled_buffer_4
  assign DB = ENABLE ? and_12_out : 1'bz;  // Controlled_Buffer controlled_buffer_5
  assign DA = ENABLE ? and_11_out : 1'bz;  // Controlled_Buffer controlled_buffer_6
  assign D9 = ENABLE ? and_10_out : 1'bz;  // Controlled_Buffer controlled_buffer_7
  assign D8 = ENABLE ? and_9_out : 1'bz;  // Controlled_Buffer controlled_buffer_8
  assign D7 = ENABLE ? and_8_out : 1'bz;  // Controlled_Buffer controlled_buffer_9
  assign D6 = ENABLE ? and_7_out : 1'bz;  // Controlled_Buffer controlled_buffer_10
  assign D5 = ENABLE ? and_6_out : 1'bz;  // Controlled_Buffer controlled_buffer_11
  assign D4 = ENABLE ? and_5_out : 1'bz;  // Controlled_Buffer controlled_buffer_12
  assign D3 = ENABLE ? and_4_out : 1'bz;  // Controlled_Buffer controlled_buffer_13
  assign D2 = ENABLE ? and_3_out : 1'bz;  // Controlled_Buffer controlled_buffer_14
  assign D1 = ENABLE ? and_2_out : 1'bz;  // Controlled_Buffer controlled_buffer_15
  assign D0 = ENABLE ? and_1_out : 1'bz;  // Controlled_Buffer controlled_buffer_16
endmodule

module A_REGISTER (
  input  CLOCK,
  input  LOAD,
  input  RESET,
  input  ENABLE,
  input  I0,
  input  I1,
  input  I2,
  input  I3,
  input  I4,
  input  I5,
  input  I6,
  input  I7,
  output L0,
  output L1,
  output L2,
  output L3,
  output L4,
  output L5,
  output L6,
  output L7,
  output O0,
  output O1,
  output O2,
  output O3,
  output O4,
  output O5,
  output O6,
  output O7
);

  Register #(.width(1)) register_1 (.D(I0), .en(LOAD), .clk(CLOCK), .Q(L0), .clr(RESET));
  Register #(.width(1)) register_2 (.D(I1), .en(LOAD), .clk(CLOCK), .Q(L1), .clr(RESET));
  Register #(.width(1)) register_3 (.D(I2), .en(LOAD), .clk(CLOCK), .Q(L2), .clr(RESET));
  Register #(.width(1)) register_4 (.D(I3), .en(LOAD), .clk(CLOCK), .Q(L3), .clr(RESET));
  Register #(.width(1)) register_5 (.D(I4), .en(LOAD), .clk(CLOCK), .Q(L4), .clr(RESET));
  Register #(.width(1)) register_6 (.D(I5), .en(LOAD), .clk(CLOCK), .Q(L5), .clr(RESET));
  Register #(.width(1)) register_7 (.D(I6), .en(LOAD), .clk(CLOCK), .Q(L6), .clr(RESET));
  Register #(.width(1)) register_8 (.D(I7), .en(LOAD), .clk(CLOCK), .Q(L7), .clr(RESET));
  assign O6 = ENABLE ? L6 : 1'bz;  // Controlled_Buffer controlled_buffer_1
  assign O7 = ENABLE ? L7 : 1'bz;  // Controlled_Buffer controlled_buffer_2
  assign O2 = ENABLE ? L2 : 1'bz;  // Controlled_Buffer controlled_buffer_3
  assign O3 = ENABLE ? L3 : 1'bz;  // Controlled_Buffer controlled_buffer_4
  assign O4 = ENABLE ? L4 : 1'bz;  // Controlled_Buffer controlled_buffer_5
  assign O5 = ENABLE ? L5 : 1'bz;  // Controlled_Buffer controlled_buffer_6
  assign O0 = ENABLE ? L0 : 1'bz;  // Controlled_Buffer controlled_buffer_7
  assign O1 = ENABLE ? L1 : 1'bz;  // Controlled_Buffer controlled_buffer_8
endmodule

module INSTRUCION_REGISTER (
  input  CLOCK,
  input  LOAD,
  input  RESET,
  input  ENABLE,
  input  I0,
  input  I1,
  input  I2,
  input  I3,
  input  I4,
  input  I5,
  input  I6,
  input  I7,
  output L0,
  output L1,
  output L2,
  output L3,
  output L4,
  output L5,
  output L6,
  output L7,
  output O0,
  output O1,
  output O2,
  output O3,
  output O4,
  output O5,
  output O6,
  output O7
);

  Register #(.width(1)) register_1 (.D(I0), .en(LOAD), .clk(CLOCK), .Q(L0), .clr(RESET));
  Register #(.width(1)) register_2 (.D(I1), .en(LOAD), .clk(CLOCK), .Q(L1), .clr(RESET));
  Register #(.width(1)) register_3 (.D(I2), .en(LOAD), .clk(CLOCK), .Q(L2), .clr(RESET));
  Register #(.width(1)) register_4 (.D(I3), .en(LOAD), .clk(CLOCK), .Q(L3), .clr(RESET));
  Register #(.width(1)) register_5 (.D(I4), .en(LOAD), .clk(CLOCK), .Q(L4), .clr(RESET));
  Register #(.width(1)) register_6 (.D(I5), .en(LOAD), .clk(CLOCK), .Q(L5), .clr(RESET));
  Register #(.width(1)) register_7 (.D(I6), .en(LOAD), .clk(CLOCK), .Q(L6), .clr(RESET));
  Register #(.width(1)) register_8 (.D(I7), .en(LOAD), .clk(CLOCK), .Q(L7), .clr(RESET));
  assign O5 = ENABLE ? L5 : 1'bz;  // Controlled_Buffer controlled_buffer_1
  assign O6 = ENABLE ? L6 : 1'bz;  // Controlled_Buffer controlled_buffer_2
  assign O7 = ENABLE ? L7 : 1'bz;  // Controlled_Buffer controlled_buffer_3
  assign O1 = ENABLE ? L1 : 1'bz;  // Controlled_Buffer controlled_buffer_4
  assign O2 = ENABLE ? L2 : 1'bz;  // Controlled_Buffer controlled_buffer_5
  assign O3 = ENABLE ? L3 : 1'bz;  // Controlled_Buffer controlled_buffer_6
  assign O4 = ENABLE ? L4 : 1'bz;  // Controlled_Buffer controlled_buffer_7
  assign O0 = ENABLE ? L0 : 1'bz;  // Controlled_Buffer controlled_buffer_8
endmodule

module B_REGISTER (
  input  CLOCK,
  input  LOAD,
  input  RESET,
  input  ENABLE,
  input  I0,
  input  I1,
  input  I2,
  input  I3,
  input  I4,
  input  I5,
  input  I6,
  input  I7,
  output L0,
  output L1,
  output L2,
  output L3,
  output L4,
  output L5,
  output L6,
  output L7,
  output O0,
  output O1,
  output O2,
  output O3,
  output O4,
  output O5,
  output O6,
  output O7
);

  Register #(.width(1)) register_1 (.D(I0), .en(LOAD), .clk(CLOCK), .Q(L0), .clr(RESET));
  Register #(.width(1)) register_2 (.D(I1), .en(LOAD), .clk(CLOCK), .Q(L1), .clr(RESET));
  Register #(.width(1)) register_3 (.D(I2), .en(LOAD), .clk(CLOCK), .Q(L2), .clr(RESET));
  Register #(.width(1)) register_4 (.D(I3), .en(LOAD), .clk(CLOCK), .Q(L3), .clr(RESET));
  Register #(.width(1)) register_5 (.D(I4), .en(LOAD), .clk(CLOCK), .Q(L4), .clr(RESET));
  Register #(.width(1)) register_6 (.D(I5), .en(LOAD), .clk(CLOCK), .Q(L5), .clr(RESET));
  Register #(.width(1)) register_7 (.D(I6), .en(LOAD), .clk(CLOCK), .Q(L6), .clr(RESET));
  Register #(.width(1)) register_8 (.D(I7), .en(LOAD), .clk(CLOCK), .Q(L7), .clr(RESET));
  assign O6 = ENABLE ? L6 : 1'bz;  // Controlled_Buffer controlled_buffer_1
  assign O7 = ENABLE ? L7 : 1'bz;  // Controlled_Buffer controlled_buffer_2
  assign O2 = ENABLE ? L2 : 1'bz;  // Controlled_Buffer controlled_buffer_3
  assign O3 = ENABLE ? L3 : 1'bz;  // Controlled_Buffer controlled_buffer_4
  assign O4 = ENABLE ? L4 : 1'bz;  // Controlled_Buffer controlled_buffer_5
  assign O5 = ENABLE ? L5 : 1'bz;  // Controlled_Buffer controlled_buffer_6
  assign O0 = ENABLE ? L0 : 1'bz;  // Controlled_Buffer controlled_buffer_7
  assign O1 = ENABLE ? L1 : 1'bz;  // Controlled_Buffer controlled_buffer_8
endmodule

module ALU (
  input  ENABLE,
  input  su,
  input  A7,
  input  A6,
  input  A5,
  input  A4,
  input  A3,
  input  A2,
  input  A1,
  input  A0,
  input  B7,
  input  B6,
  input  B5,
  input  B4,
  input  B3,
  input  B2,
  input  B1,
  input  B0,
  output L7,
  output L6,
  output L5,
  output L4,
  output L3,
  output L2,
  output L1,
  output L0,
  output E0,
  output CF,
  output ZF,
  output E1,
  output E2,
  output E3,
  output E4,
  output E5,
  output E6,
  output E7
);

  wire [7:0] xor_8_out;

  xor xor_1 (xor_8_out[7], B7, su);
  xor xor_2 (xor_8_out[6], B6, su);
  xor xor_3 (xor_8_out[5], B5, su);
  Adder adder_1 (
    .a({A7, A6, A5, A4, A3, A2, A1, A0}), .b(xor_8_out), .out({L7, L6, L5, L4, L3, L2, L1, L0}), .cin(su),
    .cout(CF));
  xor xor_4 (xor_8_out[4], B4, su);
  xor xor_5 (xor_8_out[3], B3, su);
  xor xor_6 (xor_8_out[2], B2, su);
  xor xor_7 (xor_8_out[1], B1, su);
  xor xor_8 (xor_8_out[0], B0, su);
  nor nor_1 (ZF, L0, L1, L2, L3, L4, L5, L6, L7);
  assign E0 = ENABLE ? L0 : 1'bz;  // Controlled_Buffer controlled_buffer_1
  assign E1 = ENABLE ? L1 : 1'bz;  // Controlled_Buffer controlled_buffer_2
  assign E2 = ENABLE ? L2 : 1'bz;  // Controlled_Buffer controlled_buffer_3
  assign E3 = ENABLE ? L3 : 1'bz;  // Controlled_Buffer controlled_buffer_4
  assign E4 = ENABLE ? L4 : 1'bz;  // Controlled_Buffer controlled_buffer_5
  assign E5 = ENABLE ? L5 : 1'bz;  // Controlled_Buffer controlled_buffer_6
  assign E6 = ENABLE ? L6 : 1'bz;  // Controlled_Buffer controlled_buffer_7
  assign E7 = ENABLE ? L7 : 1'bz;  // Controlled_Buffer controlled_buffer_8
endmodule

module FLAGS_REGISTER (
  input  CLOCK,
  input  LOAD,
  input  RESET,
  input  ENABLE,
  input  I0,
  input  I1,
  output L0,
  output L1,
  output O0,
  output O1
);

  Register #(.width(1)) register_1 (.D(I0), .en(LOAD), .clk(CLOCK), .Q(L0), .clr(RESET));
  Register #(.width(1)) register_2 (.D(I1), .en(LOAD), .clk(CLOCK), .Q(L1), .clr(RESET));
  assign O0 = ENABLE ? L0 : 1'bz;  // Controlled_Buffer controlled_buffer_1
  assign O1 = ENABLE ? L1 : 1'bz;  // Controlled_Buffer controlled_buffer_2
endmodule

module INSTRUCTION_DECODER (
  input  PROGRAM_MODE,
  input  ZF,
  input  CF,
  input  OP0,
  input  OP1,
  input  OP2,
  input  OP3,
  input  COLCK,
  input  CLEAR,
  output OI,
  output IO,
  output II,
  output RO,
  output RI,
  output MI,
  output FI,
  output BO,
  output BI,
  output S0,
  output S1,
  output S2,
  output S3,
  output S4,
  output S5,
  output S6,
  output S7,
  output SU,
  output EO,
  output AO,
  output AI,
  output JP,
  output CO,
  output CE,
  output HL
);

  wire decoder_4bits_1_d8, not_1_out, not_2_out, or_1_out, or_2_out, program_counter_1_l3;
  wire [2:0] program_counter_1_l0;
  wire [16:0] rom_1_data;

  or or_1 (or_1_out, CLEAR, decoder_4bits_1_d8);
  buf or_2 (or_2_out, not_1_out);  // OR_Gate
  not not_1 (not_1_out, COLCK);
  PROGRAM_COUNTER program_counter_1 (
    .CEnable(or_2_out), .CReset(or_1_out), .CLOCK(or_2_out), .L3(program_counter_1_l3),
    .L2(program_counter_1_l0[2]), .L1(program_counter_1_l0[1]), .L0(program_counter_1_l0[0]));  // open: COut, CWrite, I7, I6, I5, I4, I3, I2, I1, I0, O7, O6, O5, O4, O3, O2, O1, O0, L7, L6, L5, L4
  DECODER_4BITS decoder_4bits_1 (
    .I3(program_counter_1_l3), .I2(program_counter_1_l0[2]), .I1(program_counter_1_l0[1]),
    .I0(program_counter_1_l0[0]), .ENABLE(1'b1), .D8(decoder_4bits_1_d8), .D7(S7), .D6(S6), .D5(S5), .D4(S4),
    .D3(S3), .D2(S2), .D1(S1), .D0(S0));  // open: DF, DE, DD, DC, DB, DA, D9
  ROM #(.addrWidth(9), .dataWidth(17)) rom_1 (
    .addr({OP3, OP2, OP1, OP0, CF, ZF, program_counter_1_l0}), .data(rom_1_data));
  not not_2 (not_2_out, PROGRAM_MODE);
  assign OI = not_2_out ? rom_1_data[0] : 1'bz;  // Controlled_Buffer controlled_buffer_1
  assign IO = not_2_out ? rom_1_data[1] : 1'bz;  // Controlled_Buffer controlled_buffer_2
  assign II = not_2_out ? rom_1_data[2] : 1'bz;  // Controlled_Buffer controlled_buffer_3
  assign RO = not_2_out ? rom_1_data[3] : 1'bz;  // Controlled_Buffer controlled_buffer_4
  assign RI = not_2_out ? rom_1_data[4] : 1'bz;  // Controlled_Buffer controlled_buffer_5
  assign MI = not_2_out ? rom_1_data[5] : 1'bz;  // Controlled_Buffer controlled_buffer_6
  assign FI = not_2_out ? rom_1_data[6] : 1'bz;  // Controlled_Buffer controlled_buffer_7
  assign BO = not_2_out ? rom_1_data[7] : 1'bz;  // Controlled_Buffer controlled_buffer_8
  assign BI = not_2_out ? rom_1_data[8] : 1'bz;  // Controlled_Buffer controlled_buffer_9
  assign SU = not_2_out ? rom_1_data[9] : 1'bz;  // Controlled_Buffer controlled_buffer_10
  assign EO = not_2_out ? rom_1_data[10] : 1'bz;  // Controlled_Buffer controlled_buffer_11
  assign AO = not_2_out ? rom_1_data[11] : 1'bz;  // Controlled_Buffer controlled_buffer_12
  assign AI = not_2_out ? rom_1_data[12] : 1'bz;  // Controlled_Buffer controlled_buffer_13
  assign JP = not_2_out ? rom_1_data[13] : 1'bz;  // Controlled_Buffer controlled_buffer_14
  assign CO = not_2_out ? rom_1_data[14] : 1'bz;  // Controlled_Buffer controlled_buffer_15
  assign CE = not_2_out ? rom_1_data[15] : 1'bz;  // Controlled_Buffer controlled_buffer_16
  assign HL = not_2_out ? rom_1_data[16] : 1'bz;  // Controlled_Buffer controlled_buffer_17

  // Notes on the sheet:
  //   counter
  //   contents of rom_1 (hex, n*v repeats v):
  //   4020 800c 6*0 4020 800c 6*0 4020 800c 6*0 4020 800c 6*0 4020 800c 10000 5*0 4020 800c 10000 5*0 4020
  //   800c 10000 5*0 4020 800c 10000 5*0 4020 800c 22 1008 4*0 4020 800c 22 1008 4*0 4020 800c 22 1008 4*0
  //   4020 800c 22 1008 4*0 4020 800c 22 108 1440 0 0 0 4020 800c 22 108 1440 0 0 0 4020 800c 22 108 1440
  //   0 0 0 4020 800c 22 108 1440 0 0 0 4020 800c 22 108 1640 0 0 0 4020 800c 22 108 1640 0 0 0 4020 800c
  //   22 108 1640 0 0 0 4020 800c 22 108 1640 0 0 0 4020 800c 22 810 4*0 4020 800c 22 810 4*0 4020 800c 22
  //   810 4*0 4020 800c 22 810 4*0 4020 800c 1002 5*0 4020 800c 1002 5*0 4020 800c 1002 5*0 4020 800c 1002
  //   5*0 4020 800c 2002 5*0 4020 800c 2002 5*0 4020 800c 2002 5*0 4020 800c 2002 5*0 4020 800c 6*0 4020
  //   800c 6*0 4020 800c 2002 5*0 4020 800c 2002 5*0 4020 800c 6*0 4020 800c 2002 5*0 4020 800c 6*0 4020
  //   800c 2002 5*0 4020 800c 801 5*0 4020 800c 801 5*0 4020 800c 801 5*0 4020 800c 801 5*0 4020 800c 6*0
  //   4020 800c 6*0 4020 800c 6*0 4020 800c 6*0 4020 800c 6*0 4020 800c 6*0 4020 800c 6*0 4020 800c 6*0
  //   4020 800c 6*0 4020 800c 6*0 4020 800c 6*0 4020 800c 6*0 4020 800c 6*0 4020 800c 6*0 4020 800c 6*0
  //   4020 800c 6*0 4020 800c 6*0 4020 800c 6*0 4020 800c 6*0 4020 800c
endmodule

module DECODER_8BITS_TO_7_SEGMENTS_DISPLAY (
  input  I0,
  input  I1,
  input  I2,
  input  I3,
  input  I4,
  input  I5,
  input  I6,
  input  I7,
  output A0,
  output B0,
  output C0,
  output D0,
  output E0,
  output F0,
  output G0,
  output A1,
  output B1,
  output C1,
  output D1,
  output E1,
  output F1,
  output G1,
  output A2,
  output B2,
  output C2,
  output D2,
  output E2,
  output F2,
  output G2
);

  ROM #(.dataWidth(21)) rom_1 (
    .addr({I7, I6, I5, I4, I3, I2, I1, I0}),
    .data({G2, F2, E2, D2, C2, B2, A2, G1, F1, E1, D1, C1, B1, A1, G0, F0, E0, D0, C0, B0, A0}));

  // Notes on the sheet:
  //   contents of rom_1 (hex, n*v repeats v):
  //   fdfbf 19fbf 16dfbf 13dfbf 199fbf 1b5fbf 1f5fbf 1dfbf 1fdfbf 1bdfbf fc33f 1833f 16c33f 13c33f 19833f
  //   1b433f 1f433f 1c33f 1fc33f 1bc33f fedbf 1adbf 16edbf 13edbf 19adbf 1b6dbf 1f6dbf 1edbf 1fedbf 1bedbf
  //   fe7bf 1a7bf 16e7bf 13e7bf 19a7bf 1b67bf 1f67bf 1e7bf 1fe7bf 1be7bf ff33f 1b33f 16f33f 13f33f 19b33f
  //   1b733f 1f733f 1f33f 1ff33f 1bf33f ff6bf 1b6bf 16f6bf 13f6bf 19b6bf 1b76bf 1f76bf 1f6bf 1ff6bf 1bf6bf
  //   ffebf 1bebf 16febf 13febf 19bebf 1b7ebf 1f7ebf 1febf 1ffebf 1bfebf fc3bf 183bf 16c3bf 13c3bf 1983bf
  //   1b43bf 1f43bf 1c3bf 1fc3bf 1bc3bf fffbf 1bfbf 16ffbf 13ffbf 19bfbf 1b7fbf 1f7fbf 1ffbf 1fffbf 1bffbf
  //   ff7bf 1b7bf 16f7bf 13f7bf 19b7bf 1b77bf 1f77bf 1f7bf 1ff7bf 1bf7bf fdf86 19f86 16df86 13df86 199f86
  //   1b5f86 1f5f86 1df86 1fdf86 1bdf86 fc306 18306 16c306 13c306 198306 1b4306 1f4306 1c306 1fc306 1bc306
  //   fed86 1ad86 16ed86 13ed86 19ad86 1b6d86 1f6d86 1ed86 1fed86 1bed86 fe786 1a786 16e786 13e786 19a786
  //   1b6786 1f6786 1e786 1fe786 1be786 ff306 1b306 16f306 13f306 19b306 1b7306 1f7306 1f306 1ff306 1bf306
  //   ff686 1b686 16f686 13f686 19b686 1b7686 1f7686 1f686 1ff686 1bf686 ffe86 1be86 16fe86 13fe86 19be86
  //   1b7e86 1f7e86 1fe86 1ffe86 1bfe86 fc386 18386 16c386 13c386 198386 1b4386 1f4386 1c386 1fc386 1bc386
  //   fff86 1bf86 16ff86 13ff86 19bf86 1b7f86 1f7f86 1ff86 1fff86 1bff86 ff786 1b786 16f786 13f786 19b786
  //   1b7786 1f7786 1f786 1ff786 1bf786 fdfdb 19fdb 16dfdb 13dfdb 199fdb 1b5fdb 1f5fdb 1dfdb 1fdfdb 1bdfdb
  //   fc35b 1835b 16c35b 13c35b 19835b 1b435b 1f435b 1c35b 1fc35b 1bc35b feddb 1addb 16eddb 13eddb 19addb
  //   1b6ddb 1f6ddb 1eddb 1feddb 1beddb fe7db 1a7db 16e7db 13e7db 19a7db 1b67db 1f67db 1e7db 1fe7db 1be7db
  //   ff35b 1b35b 16f35b 13f35b 19b35b 1b735b 1f735b 1f35b 1ff35b 1bf35b ff6db 1b6db 16f6db 13f6db 19b6db
  //   1b76db
endmodule
