// Logisim project examples.circ as structural Verilog
module registro_8bits_test (
  input  MANUAL_PROGRAMING,
  input  in_2,
  input  in_3,
  input  PROGRAM_MODE,
  input  in_5,
  input  in_6,
  input  in_7,
  input  in_8,
  input  in_9,
  input  in_10,
  input  in_11,
  input  in_12,
  input  in_13,
  input  in_14,
  input  in_15,
  input  in_16,
  input  in_17,
  input  in_18,
  input  in_19,
  input  in_20,
  input  in_21,
  input  in_22,
  input  in_23,
  input  in_24,
  input  in_25,
  input  in_26,
  input  in_27,
  input  in_28,
  output out_29,
  output out_30
);

  wire AI, alu_1_cf, alu_1_l0, alu_1_l1, alu_1_l2, alu_1_l3, alu_1_l4, alu_1_l5, alu_1_l6, alu_1_l7,
       alu_1_zf, AO, B_CLK, BI, BO, CE, CLK, clock_1_out, CO, EO, FI, flags_rgister_1_l0, flags_rgister_1_l1,
       HL, II, instruccion_decoder_1_s0, instruccion_decoder_1_s1, instruccion_decoder_1_s2,
       instruccion_decoder_1_s3, instruccion_decoder_1_s4, instruccion_decoder_1_s5,
       instruccion_decoder_1_s6, instruccion_decoder_1_s7, instruccion_register_1_l0,
       instruccion_register_1_l1, instruccion_register_1_l2, instruccion_register_1_l3,
       instruccion_register_1_l4, instruccion_register_1_l5, instruccion_register_1_l6,
       instruccion_register_1_l7, IO, JP, mar_1_l0, mar_1_l1, mar_1_l2, mar_1_l3, mar_1_l4, mar_1_l5,
       mar_1_l6, mar_1_l7, mar_1_l8, mar_1_l9, mar_1_la, mar_1_lb, mar_1_lc, mar_1_ld, mar_1_le, mar_1_lf,
       MI, OI, or_1_out, or_2_out, program_counter_1_l0, program_counter_1_l1, program_counter_1_l2,
       program_counter_1_l3, program_counter_1_l4, program_counter_1_l5, program_counter_1_l6,
       program_counter_1_l7, registro_8bit_1_l0, registro_8bit_1_l1, registro_8bit_1_l2, registro_8bit_1_l3,
       registro_8bit_1_l4, registro_8bit_1_l5, registro_8bit_1_l6, registro_8bit_1_l7, registro_8bits_b_1_l0,
       registro_8bits_b_1_l1, registro_8bits_b_1_l2, registro_8bits_b_1_l3, registro_8bits_b_1_l4,
       registro_8bits_b_1_l5, registro_8bits_b_1_l6, registro_8bits_b_1_l7, REST, RI, RO, SU;
  wire [3:0] registro_8bit_2_l0, registro_8bit_2_l4;
  wire [7:0] instruccion_register_1_o0, ram_1_dout;
  wire [15:0] mar_1_addrs;

  or or_1 (or_1_out, RO, CLK);
  Clock clock_1 (.out(clock_1_out));
  DotMatrix #(.matrixcols(16), .matrixrows(1)) dotmatrix_1 (
    .col0(mar_1_l0), .col1(mar_1_l1), .col2(mar_1_l2), .col3(mar_1_l3), .col4(mar_1_l4), .col5(mar_1_l5),
    .col6(mar_1_l6), .col7(mar_1_l7), .col8(mar_1_l8), .col9(mar_1_l9), .col10(mar_1_la), .col11(mar_1_lb),
    .col12(mar_1_lc), .col13(mar_1_ld), .col14(mar_1_le), .col15(mar_1_lf));
  RAM #(.addrWidth(16)) ram_1 (
    .addr(mar_1_addrs), .we(RI), .oe(RO), .clk(or_1_out), .din(instruccion_register_1_o0), .dout(ram_1_dout));
  INSTRUCCION_REGISTER instruccion_register_1 (
    .ENABLE(IO), .I0(instruccion_register_1_o0[0]), .I1(instruccion_register_1_o0[1]),
    .I2(instruccion_register_1_o0[2]), .I3(instruccion_register_1_o0[3]), .I4(instruccion_register_1_o0[4]),
    .I5(instruccion_register_1_o0[5]), .I6(instruccion_register_1_o0[6]), .I7(instruccion_register_1_o0[7]),
    .CLOCK(CLK), .LOAD(II), .RESET(REST), .O0(instruccion_register_1_o0[0]),
    .O1(instruccion_register_1_o0[1]), .O2(instruccion_register_1_o0[2]), .O3(instruccion_register_1_o0[3]),
    .L0(instruccion_register_1_l0), .L1(instruccion_register_1_l1), .L2(instruccion_register_1_l2),
    .L3(instruccion_register_1_l3), .L4(instruccion_register_1_l4), .L5(instruccion_register_1_l5),
    .L6(instruccion_register_1_l6), .L7(instruccion_register_1_l7));  // open: O4, O5, O6, O7
  DotMatrix #(.matrixcols(4), .matrixrows(1)) dotmatrix_2 (
    .col0(instruccion_register_1_l7), .col1(instruccion_register_1_l6), .col2(instruccion_register_1_l5),
    .col3(instruccion_register_1_l4));
  INSTRUCCION_DECODER instruccion_decoder_1 (
    .PROGRAM_MODE(PROGRAM_MODE), .ZF(out_30), .CF(out_29), .OP0(instruccion_register_1_l4),
    .OP1(instruccion_register_1_l5), .OP2(instruccion_register_1_l6), .OP3(instruccion_register_1_l7),
    .COLCK(CLK), .CLEAR(REST), .HL(HL), .OI(OI), .IO(IO), .II(II), .RO(RO), .RI(RI), .MI(MI), .FI(FI),
    .BO(BO), .BI(BI), .SU(SU), .EO(EO), .AO(AO), .AI(AI), .JP(JP), .CO(CO), .CE(CE),
    .S0(instruccion_decoder_1_s0), .S1(instruccion_decoder_1_s1), .S2(instruccion_decoder_1_s2),
    .S3(instruccion_decoder_1_s3), .S4(instruccion_decoder_1_s4), .S5(instruccion_decoder_1_s5),
    .S6(instruccion_decoder_1_s6), .S7(instruccion_decoder_1_s7));
  or or_2 (or_2_out, clock_1_out, B_CLK);
  DotMatrix #(.matrixcols(4), .matrixrows(1)) dotmatrix_3 (
    .col0(instruccion_register_1_o0[3]), .col1(instruccion_register_1_o0[2]),
    .col2(instruccion_register_1_o0[1]), .col3(instruccion_register_1_o0[0]));
  MAR mar_1 (
    .ENABLE(1'b1), .I0(instruccion_register_1_o0[0]), .I1(instruccion_register_1_o0[1]),
    .I2(instruccion_register_1_o0[2]), .I3(instruccion_register_1_o0[3]), .CLOCK(CLK), .LOAD(MI),
    .RESET(REST), .L0(mar_1_l0), .L1(mar_1_l1), .L2(mar_1_l2), .L3(mar_1_l3), .L4(mar_1_l4), .L5(mar_1_l5),
    .L6(mar_1_l6), .L7(mar_1_l7), .L8(mar_1_l8), .L9(mar_1_l9), .LA(mar_1_la), .LB(mar_1_lb), .LC(mar_1_lc),
    .LD(mar_1_ld), .LE(mar_1_le), .LF(mar_1_lf), .ADDRS(mar_1_addrs));  // open: I4, I5, I6, I7
  DotMatrix #(.matrixcols(4), .matrixrows(1)) dotmatrix_4 (
    .col0(instruccion_register_1_l3), .col1(instruccion_register_1_l2), .col2(instruccion_register_1_l1),
    .col3(instruccion_register_1_l0));
  DotMatrix #(.matrixcols(8), .matrixrows(1)) dotmatrix_5 (
    .col0(instruccion_decoder_1_s0), .col1(instruccion_decoder_1_s1), .col2(instruccion_decoder_1_s2),
    .col3(instruccion_decoder_1_s3), .col4(instruccion_decoder_1_s4), .col5(instruccion_decoder_1_s5),
    .col6(instruccion_decoder_1_s6), .col7(instruccion_decoder_1_s7));
  Button CLCK (.out(B_CLK));
  Button RESET (.out(REST));
  and and_1 (CLK, or_2_out, ~HL);  // AND_Gate
  assign instruccion_register_1_o0[0] = RO ? ram_1_dout[0] : 1'bz;  // Controlled_Buffer controlled_buffer_1
  assign instruccion_register_1_o0[1] = RO ? ram_1_dout[1] : 1'bz;  // Controlled_Buffer controlled_buffer_2
  assign instruccion_register_1_o0[2] = RO ? ram_1_dout[2] : 1'bz;  // Controlled_Buffer controlled_buffer_3
  assign instruccion_register_1_o0[3] = RO ? ram_1_dout[3] : 1'bz;  // Controlled_Buffer controlled_buffer_4
  assign instruccion_register_1_o0[4] = RO ? ram_1_dout[4] : 1'bz;  // Controlled_Buffer controlled_buffer_5
  assign instruccion_register_1_o0[5] = RO ? ram_1_dout[5] : 1'bz;  // Controlled_Buffer controlled_buffer_6
  assign instruccion_register_1_o0[6] = RO ? ram_1_dout[6] : 1'bz;  // Controlled_Buffer controlled_buffer_7
  assign instruccion_register_1_o0[7] = RO ? ram_1_dout[7] : 1'bz;  // Controlled_Buffer controlled_buffer_8
  DotMatrix #(.matrixcols(8), .matrixrows(1)) dotmatrix_6 (
    .col0(instruccion_register_1_o0[7]), .col1(instruccion_register_1_o0[6]),
    .col2(instruccion_register_1_o0[5]), .col3(instruccion_register_1_o0[4]),
    .col4(instruccion_register_1_o0[3]), .col5(instruccion_register_1_o0[2]),
    .col6(instruccion_register_1_o0[1]), .col7(instruccion_register_1_o0[0]));
  assign instruccion_register_1_o0[0] = in_11 ? in_20 : 1'bz;  // Controlled_Buffer controlled_buffer_9
  assign instruccion_register_1_o0[1] = in_11 ? in_19 : 1'bz;  // Controlled_Buffer controlled_buffer_10
  assign instruccion_register_1_o0[2] = in_11 ? in_18 : 1'bz;  // Controlled_Buffer controlled_buffer_11
  assign instruccion_register_1_o0[3] = in_11 ? in_17 : 1'bz;  // Controlled_Buffer controlled_buffer_12
  assign instruccion_register_1_o0[4] = in_11 ? in_16 : 1'bz;  // Controlled_Buffer controlled_buffer_13
  assign instruccion_register_1_o0[5] = in_11 ? in_15 : 1'bz;  // Controlled_Buffer controlled_buffer_14
  assign instruccion_register_1_o0[6] = in_11 ? in_14 : 1'bz;  // Controlled_Buffer controlled_buffer_15
  assign instruccion_register_1_o0[7] = in_11 ? in_13 : 1'bz;  // Controlled_Buffer controlled_buffer_16
  DotMatrix #(.matrixcols(8), .matrixrows(1)) dotmatrix_7 (
    .col0(instruccion_register_1_o0[7]), .col1(instruccion_register_1_o0[6]),
    .col2(instruccion_register_1_o0[5]), .col3(instruccion_register_1_o0[4]),
    .col4(instruccion_register_1_o0[3]), .col5(instruccion_register_1_o0[2]),
    .col6(instruccion_register_1_o0[1]), .col7(instruccion_register_1_o0[0]));
  assign MI = MANUAL_PROGRAMING ? in_2 : 1'bz;  // Controlled_Buffer controlled_buffer_17
  assign RI = MANUAL_PROGRAMING ? in_6 : 1'bz;  // Controlled_Buffer controlled_buffer_18
  assign RO = MANUAL_PROGRAMING ? in_8 : 1'bz;  // Controlled_Buffer controlled_buffer_19
  assign II = MANUAL_PROGRAMING ? in_9 : 1'bz;  // Controlled_Buffer controlled_buffer_20
  assign IO = MANUAL_PROGRAMING ? in_10 : 1'bz;  // Controlled_Buffer controlled_buffer_21
  assign OI = MANUAL_PROGRAMING ? in_21 : 1'bz;  // Controlled_Buffer controlled_buffer_22
  assign BI = MANUAL_PROGRAMING ? in_23 : 1'bz;  // Controlled_Buffer controlled_buffer_23
  assign BO = MANUAL_PROGRAMING ? in_25 : 1'bz;  // Controlled_Buffer controlled_buffer_24
  PROGRAM_COUNTER program_counter_1 (
    .COut(CO), .CEnable(CE), .CWrite(JP), .CReset(REST), .CLOCK(CLK), .I3(instruccion_register_1_o0[3]),
    .I2(instruccion_register_1_o0[2]), .I1(instruccion_register_1_o0[1]), .I0(instruccion_register_1_o0[0]),
    .O3(instruccion_register_1_o0[3]), .O2(instruccion_register_1_o0[2]), .O1(instruccion_register_1_o0[1]),
    .O0(instruccion_register_1_o0[0]), .L7(program_counter_1_l7), .L6(program_counter_1_l6),
    .L5(program_counter_1_l5), .L4(program_counter_1_l4), .L3(program_counter_1_l3),
    .L2(program_counter_1_l2), .L1(program_counter_1_l1), .L0(program_counter_1_l0));  // open: I7, I6, I5, I4, O7, O6, O5, O4
  DotMatrix #(.matrixcols(8), .matrixrows(1)) dotmatrix_8 (
    .col0(registro_8bit_1_l7), .col1(registro_8bit_1_l6), .col2(registro_8bit_1_l5),
    .col3(registro_8bit_1_l4), .col4(registro_8bit_1_l3), .col5(registro_8bit_1_l2),
    .col6(registro_8bit_1_l1), .col7(registro_8bit_1_l0));
  DotMatrix #(.matrixcols(8), .matrixrows(1)) dotmatrix_9 (
    .col0(registro_8bits_b_1_l7), .col1(registro_8bits_b_1_l6), .col2(registro_8bits_b_1_l5),
    .col3(registro_8bits_b_1_l4), .col4(registro_8bits_b_1_l3), .col5(registro_8bits_b_1_l2),
    .col6(registro_8bits_b_1_l1), .col7(registro_8bits_b_1_l0));
  DotMatrix #(.matrixcols(8), .matrixrows(1)) dotmatrix_10 (
    .col0(program_counter_1_l0), .col1(program_counter_1_l1), .col2(program_counter_1_l2),
    .col3(program_counter_1_l3), .col4(program_counter_1_l4), .col5(program_counter_1_l5),
    .col6(program_counter_1_l6), .col7(program_counter_1_l7));
  registro_8bit registro_8bit_1 (
    .ENABLE(AO), .I0(instruccion_register_1_o0[0]), .I1(instruccion_register_1_o0[1]),
    .I2(instruccion_register_1_o0[2]), .I3(instruccion_register_1_o0[3]), .I4(instruccion_register_1_o0[4]),
    .I5(instruccion_register_1_o0[5]), .I6(instruccion_register_1_o0[6]), .I7(instruccion_register_1_o0[7]),
    .CLOCK(CLK), .LOAD(AI), .RESET(REST), .O0(instruccion_register_1_o0[0]),
    .O1(instruccion_register_1_o0[1]), .O2(instruccion_register_1_o0[2]), .O3(instruccion_register_1_o0[3]),
    .O4(instruccion_register_1_o0[4]), .O5(instruccion_register_1_o0[5]), .O6(instruccion_register_1_o0[6]),
    .O7(instruccion_register_1_o0[7]), .L0(registro_8bit_1_l0), .L1(registro_8bit_1_l1),
    .L2(registro_8bit_1_l2), .L3(registro_8bit_1_l3), .L4(registro_8bit_1_l4), .L5(registro_8bit_1_l5),
    .L6(registro_8bit_1_l6), .L7(registro_8bit_1_l7));
  registro_8bits_B registro_8bits_b_1 (
    .ENABLE(BO), .I0(instruccion_register_1_o0[0]), .I1(instruccion_register_1_o0[1]),
    .I2(instruccion_register_1_o0[2]), .I3(instruccion_register_1_o0[3]), .I4(instruccion_register_1_o0[4]),
    .I5(instruccion_register_1_o0[5]), .I6(instruccion_register_1_o0[6]), .I7(instruccion_register_1_o0[7]),
    .CLOCK(CLK), .LOAD(BI), .RESET(REST), .O0(instruccion_register_1_o0[0]),
    .O1(instruccion_register_1_o0[1]), .O2(instruccion_register_1_o0[2]), .O3(instruccion_register_1_o0[3]),
    .O4(instruccion_register_1_o0[4]), .O5(instruccion_register_1_o0[5]), .O6(instruccion_register_1_o0[6]),
    .O7(instruccion_register_1_o0[7]), .L0(registro_8bits_b_1_l0), .L1(registro_8bits_b_1_l1),
    .L2(registro_8bits_b_1_l2), .L3(registro_8bits_b_1_l3), .L4(registro_8bits_b_1_l4),
    .L5(registro_8bits_b_1_l5), .L6(registro_8bits_b_1_l6), .L7(registro_8bits_b_1_l7));
  DotMatrix #(.matrixcols(8), .matrixrows(1)) dotmatrix_11 (
    .col0(registro_8bit_2_l4[3]), .col1(registro_8bit_2_l4[2]), .col2(registro_8bit_2_l4[1]),
    .col3(registro_8bit_2_l4[0]), .col4(registro_8bit_2_l0[3]), .col5(registro_8bit_2_l0[2]),
    .col6(registro_8bit_2_l0[1]), .col7(registro_8bit_2_l0[0]));
  Hex_Digit_Display hex_digit_display_1 (.value(registro_8bit_2_l4));  // open: dp
  assign CO = MANUAL_PROGRAMING ? in_3 : 1'bz;  // Controlled_Buffer controlled_buffer_25
  assign JP = MANUAL_PROGRAMING ? in_5 : 1'bz;  // Controlled_Buffer controlled_buffer_26
  assign CE = MANUAL_PROGRAMING ? in_7 : 1'bz;  // Controlled_Buffer controlled_buffer_27
  assign SU = MANUAL_PROGRAMING ? in_12 : 1'bz;  // Controlled_Buffer controlled_buffer_28
  assign EO = MANUAL_PROGRAMING ? in_22 : 1'bz;  // Controlled_Buffer controlled_buffer_29
  assign AI = MANUAL_PROGRAMING ? in_24 : 1'bz;  // Controlled_Buffer controlled_buffer_30
  assign AO = MANUAL_PROGRAMING ? in_26 : 1'bz;  // Controlled_Buffer controlled_buffer_31
  assign FI = MANUAL_PROGRAMING ? in_27 : 1'bz;  // Controlled_Buffer controlled_buffer_32
  assign HL = MANUAL_PROGRAMING ? in_28 : 1'bz;  // Controlled_Buffer controlled_buffer_33
  registro_8bit registro_8bit_2 (
    .I0(instruccion_register_1_o0[0]), .I1(instruccion_register_1_o0[1]), .I2(instruccion_register_1_o0[2]),
    .I3(instruccion_register_1_o0[3]), .I4(instruccion_register_1_o0[4]), .I5(instruccion_register_1_o0[5]),
    .I6(instruccion_register_1_o0[6]), .I7(instruccion_register_1_o0[7]), .CLOCK(CLK), .LOAD(OI),
    .RESET(REST), .L0(registro_8bit_2_l0[0]), .L1(registro_8bit_2_l0[1]), .L2(registro_8bit_2_l0[2]),
    .L3(registro_8bit_2_l0[3]), .L4(registro_8bit_2_l4[0]), .L5(registro_8bit_2_l4[1]),
    .L6(registro_8bit_2_l4[2]), .L7(registro_8bit_2_l4[3]));  // open: ENABLE, O0, O1, O2, O3, O4, O5, O6, O7
  Hex_Digit_Display hex_digit_display_2 (.value(registro_8bit_2_l0));  // open: dp
  ALU alu_1 (
    .ENABLE(EO), .A7(registro_8bit_1_l7), .B7(registro_8bits_b_1_l7), .A6(registro_8bit_1_l6),
    .B6(registro_8bits_b_1_l6), .A5(registro_8bit_1_l5), .B5(registro_8bits_b_1_l5), .A4(registro_8bit_1_l4),
    .B4(registro_8bits_b_1_l4), .A3(registro_8bit_1_l3), .B3(registro_8bits_b_1_l3), .A2(registro_8bit_1_l2),
    .B2(registro_8bits_b_1_l2), .A1(registro_8bit_1_l1), .B1(registro_8bits_b_1_l1), .A0(registro_8bit_1_l0),
    .B0(registro_8bits_b_1_l0), .su(SU), .E0(instruccion_register_1_o0[0]),
    .E1(instruccion_register_1_o0[1]), .E2(instruccion_register_1_o0[2]), .E3(instruccion_register_1_o0[3]),
    .E4(instruccion_register_1_o0[4]), .E5(instruccion_register_1_o0[5]), .E6(instruccion_register_1_o0[6]),
    .E7(instruccion_register_1_o0[7]), .CF(alu_1_cf), .ZF(alu_1_zf), .L7(alu_1_l7), .L6(alu_1_l6),
    .L5(alu_1_l5), .L4(alu_1_l4), .L3(alu_1_l3), .L2(alu_1_l2), .L1(alu_1_l1), .L0(alu_1_l0));
  DotMatrix #(.matrixcols(8), .matrixrows(1)) dotmatrix_12 (
    .col0(alu_1_l0), .col1(alu_1_l1), .col2(alu_1_l2), .col3(alu_1_l3), .col4(alu_1_l4), .col5(alu_1_l5),
    .col6(alu_1_l6), .col7(alu_1_l7));
  DotMatrix #(.matrixcols(2), .matrixrows(1)) dotmatrix_13 (.col0(flags_rgister_1_l0), .col1(flags_rgister_1_l1));
  flags_rgister flags_rgister_1 (
    .I0(alu_1_cf), .I1(alu_1_zf), .CLOCK(CLK), .LOAD(FI), .RESET(REST), .ENABLE(1'b1),
    .L0(flags_rgister_1_l0), .L1(flags_rgister_1_l1), .O0(out_29), .O1(out_30));

  // Other names for the same wires on the sheet: CF = out_29; ZF = out_30

  // Notes on the sheet:
  //   PC
  //   8bits-register-A
  //   OutPut-register
endmodule

module INSTRUCCION_DECODER (
  input  PROGRAM_MODE,
  input  ZF,
  input  CF,
  input  OP0,
  input  OP1,
  input  OP2,
  input  OP3,
  input  COLCK,
  input  CLEAR,
  output OI,
  output IO,
  output II,
  output RO,
  output RI,
  output MI,
  output FI,
  output BO,
  output BI,
  output S0,
  output S1,
  output S2,
  output S3,
  output S4,
  output S5,
  output S6,
  output S7,
  output SU,
  output EO,
  output AO,
  output AI,
  output JP,
  output CO,
  output CE,
  output HL
);

  wire clock_1_out, decoder_4bits_1_d8, not_2_out, not_3_out, or_1_out, or_2_out, program_counter_1_l3;
  wire [2:0] program_counter_1_l0;
  wire [16:0] rom_1_data;

  Clock clock_1 (.out(clock_1_out));
  // NOT_Gate not_1 has open pins: in=clock_1_out, out=open
  or or_1 (or_1_out, CLEAR, decoder_4bits_1_d8);
  buf or_2 (or_2_out, not_2_out);  // OR_Gate
  PROGRAM_COUNTER program_counter_1 (
    .CEnable(or_2_out), .CReset(or_1_out), .CLOCK(or_2_out), .L3(program_counter_1_l3),
    .L2(program_counter_1_l0[2]), .L1(program_counter_1_l0[1]), .L0(program_counter_1_l0[0]));  // open: COut, CWrite, I7, I6, I5, I4, I3, I2, I1, I0, O7, O6, O5, O4, O3, O2, O1, O0, L7, L6, L5, L4
  not not_2 (not_2_out, COLCK);
  decoder_4bits decoder_4bits_1 (
    .I3(program_counter_1_l3), .I2(program_counter_1_l0[2]), .I1(program_counter_1_l0[1]),
    .I0(program_counter_1_l0[0]), .ENABLE(1'b1), .D8(decoder_4bits_1_d8), .D7(S7), .D6(S6), .D5(S5), .D4(S4),
    .D3(S3), .D2(S2), .D1(S1), .D0(S0));  // open: DF, DE, DD, DC, DB, DA, D9
  ROM #(.addrWidth(9), .dataWidth(17)) rom_1 (
    .addr({OP3, OP2, OP1, OP0, CF, ZF, program_counter_1_l0}), .data(rom_1_data));
  not not_3 (not_3_out, PROGRAM_MODE);
  assign OI = not_3_out ? rom_1_data[0] : 1'bz;  // Controlled_Buffer controlled_buffer_1
  assign IO = not_3_out ? rom_1_data[1] : 1'bz;  // Controlled_Buffer controlled_buffer_2
  assign II = not_3_out ? rom_1_data[2] : 1'bz;  // Controlled_Buffer controlled_buffer_3
  assign RO = not_3_out ? rom_1_data[3] : 1'bz;  // Controlled_Buffer controlled_buffer_4
  assign RI = not_3_out ? rom_1_data[4] : 1'bz;  // Controlled_Buffer controlled_buffer_5
  assign MI = not_3_out ? rom_1_data[5] : 1'bz;  // Controlled_Buffer controlled_buffer_6
  assign FI = not_3_out ? rom_1_data[6] : 1'bz;  // Controlled_Buffer controlled_buffer_7
  assign BO = not_3_out ? rom_1_data[7] : 1'bz;  // Controlled_Buffer controlled_buffer_8
  assign BI = not_3_out ? rom_1_data[8] : 1'bz;  // Controlled_Buffer controlled_buffer_9
  assign SU = not_3_out ? rom_1_data[9] : 1'bz;  // Controlled_Buffer controlled_buffer_10
  assign EO = not_3_out ? rom_1_data[10] : 1'bz;  // Controlled_Buffer controlled_buffer_11
  assign AO = not_3_out ? rom_1_data[11] : 1'bz;  // Controlled_Buffer controlled_buffer_12
  assign AI = not_3_out ? rom_1_data[12] : 1'bz;  // Controlled_Buffer controlled_buffer_13
  assign JP = not_3_out ? rom_1_data[13] : 1'bz;  // Controlled_Buffer controlled_buffer_14
  assign CO = not_3_out ? rom_1_data[14] : 1'bz;  // Controlled_Buffer controlled_buffer_15
  assign CE = not_3_out ? rom_1_data[15] : 1'bz;  // Controlled_Buffer controlled_buffer_16
  assign HL = not_3_out ? rom_1_data[16] : 1'bz;  // Controlled_Buffer controlled_buffer_17

  // Notes on the sheet:
  //   counter
  //   contents of rom_1 (hex, n*v repeats v):
  //   4020 800c 6*0 4020 800c 6*0 4020 800c 6*0 4020 800c 6*0 4020 800c 10000 5*0 4020 800c 10000 5*0 4020
  //   800c 10000 5*0 4020 800c 10000 5*0 4020 800c 22 1008 4*0 4020 800c 22 1008 4*0 4020 800c 22 1008 4*0
  //   4020 800c 22 1008 4*0 4020 800c 22 108 1400 0 0 0 4020 800c 22 108 1400 0 0 0 4020 800c 22 108 1400
  //   0 0 0 4020 800c 22 108 1400 0 0 0 4020 800c 801 5*0 4020 800c 801 5*0 4020 800c 801 5*0 4020 800c
  //   801 5*0 4020 800c 6*0 4020 800c 6*0 4020 800c 6*0 4020 800c 6*0 4020 800c 6*0 4020 800c 6*0 4020
  //   800c 6*0 4020 800c 6*0 4020 800c 6*0 4020 800c 6*0 4020 800c 6*0 4020 800c 6*0 4020 800c 6*0 4020
  //   800c 6*0 4020 800c 6*0 4020 800c 6*0 4020 800c 6*0 4020 800c 6*0 4020 800c 6*0 4020 800c 6*0 4020
  //   800c 6*0 4020 800c 6*0 4020 800c 6*0 4020 800c 6*0 4020 800c 6*0 4020 800c 6*0 4020 800c 6*0 4020
  //   800c
endmodule

module bus_and_rgisters (
  input  in_1,
  input  in_2,
  input  in_3,
  input  in_4,
  input  in_5,
  input  in_6,
  input  in_7,
  input  in_8,
  input  in_9,
  input  in_10,
  input  in_11,
  input  in_12,
  input  in_13,
  input  in_14,
  input  in_15,
  input  in_16,
  input  in_17,
  output out_18,
  output out_19,
  output out_20,
  output out_21,
  output out_22,
  output out_23,
  output out_24,
  output out_25,
  output out_26,
  output out_27
);

  wire clock_1_out, j_k_ff_1_q, j_k_ff_2_q, j_k_ff_3_q, j_k_ff_4_q, j_k_ff_5_q, j_k_ff_6_q, j_k_ff_7_q,
       j_k_ff_8_q, or_1_out;
  wire [2:0] ram_1_dout;
  wire [7:0] j_k_ff_1_qn;

  Clock clock_1 (.out(clock_1_out));
  J_K_Flip_Flop j_k_ff_1 (
    .J(clock_1_out), .K(clock_1_out), .clk(clock_1_out), .Q(j_k_ff_1_q), .Qn(j_k_ff_1_qn[0]), .reset(in_7));  // open: preset
  J_K_Flip_Flop j_k_ff_2 (
    .J(j_k_ff_1_q), .K(j_k_ff_1_q), .clk(j_k_ff_1_q), .Q(j_k_ff_2_q), .Qn(j_k_ff_1_qn[1]), .reset(in_7));  // open: preset
  J_K_Flip_Flop j_k_ff_3 (
    .J(j_k_ff_2_q), .K(j_k_ff_2_q), .clk(j_k_ff_2_q), .Q(j_k_ff_3_q), .Qn(j_k_ff_1_qn[2]), .reset(in_7));  // open: preset
  J_K_Flip_Flop j_k_ff_4 (
    .J(j_k_ff_3_q), .K(j_k_ff_3_q), .clk(j_k_ff_3_q), .Q(j_k_ff_4_q), .Qn(j_k_ff_1_qn[3]), .reset(in_7));  // open: preset
  J_K_Flip_Flop j_k_ff_5 (
    .J(j_k_ff_4_q), .K(j_k_ff_4_q), .clk(j_k_ff_4_q), .Q(j_k_ff_5_q), .Qn(j_k_ff_1_qn[4]), .reset(in_7));  // open: preset
  J_K_Flip_Flop j_k_ff_6 (
    .J(j_k_ff_5_q), .K(j_k_ff_5_q), .clk(j_k_ff_5_q), .Q(j_k_ff_6_q), .Qn(j_k_ff_1_qn[5]), .reset(in_7));  // open: preset
  J_K_Flip_Flop j_k_ff_7 (
    .J(j_k_ff_6_q), .K(j_k_ff_6_q), .clk(j_k_ff_6_q), .Q(j_k_ff_7_q), .Qn(j_k_ff_1_qn[6]), .reset(in_7));  // open: preset
  J_K_Flip_Flop j_k_ff_8 (
    .J(j_k_ff_7_q), .K(j_k_ff_7_q), .clk(j_k_ff_7_q), .Q(j_k_ff_8_q), .Qn(j_k_ff_1_qn[7]), .reset(in_7));  // open: preset
  DotMatrix #(.matrixcols(8), .matrixrows(1)) dotmatrix_1 (
    .col0(j_k_ff_1_qn[7]), .col1(j_k_ff_1_qn[6]), .col2(j_k_ff_1_qn[5]), .col3(j_k_ff_1_qn[4]),
    .col4(j_k_ff_1_qn[3]), .col5(j_k_ff_1_qn[2]), .col6(j_k_ff_1_qn[1]), .col7(j_k_ff_1_qn[0]));
  ROM rom_1 ();  // open: addr, data
  RAM #(.addrWidth(3), .clearpin("true"), .dataWidth(3)) ram_1 (
    .addr({in_15, in_14, in_13}), .oe(in_16), .clk(or_1_out), .dout(ram_1_dout));  // open: we, din, clr
  or or_1 (or_1_out, in_16, in_17);
  Adder adder_1 (
    .a(j_k_ff_1_qn), .b(j_k_ff_1_qn), .out({out_27, out_26, out_25, out_24, out_23, out_22, out_21, out_20}));  // open: cin, cout
  T_Flip_Flop t_ff_1 ();  // open: T, clk, Q, Qn, reset, preset
  D_Flip_Flop d_ff_1 ();  // open: D, clk, Q, Qn, preset, reset
  J_K_Flip_Flop j_k_ff_9 (.J(in_2), .K(in_3), .clk(in_4), .Q(out_18), .Qn(out_19), .preset(in_1), .reset(in_5));
  S_R_Flip_Flop s_r_ff_1 (.S(in_8), .R(in_9), .clk(in_10), .reset(in_11), .preset(in_6));  // open: Q, Qn
endmodule

module counterr (
);

  PROGRAM_COUNTER program_counter_1 ();  // open: COut, CEnable, CWrite, CReset, CLOCK, I7, I6, I5, I4, I3, I2, I1, I0, O7, O6, O5, O4, O3, O2, O1, O0, L7, L6, L5, L4, L3, L2, L1, L0
endmodule

module registro_8bit (
  input  CLOCK,
  input  LOAD,
  input  RESET,
  input  ENABLE,
  input  I0,
  input  I1,
  input  I2,
  input  I3,
  input  I4,
  input  I5,
  input  I6,
  input  I7,
  output L0,
  output L1,
  output L2,
  output L3,
  output L4,
  output L5,
  output L6,
  output L7,
  output O0,
  output O1,
  output O2,
  output O3,
  output O4,
  output O5,
  output O6,
  output O7
);

  Register #(.width(1)) register_1 (.D(I0), .en(LOAD), .clk(CLOCK), .Q(L0), .clr(RESET));
  Register #(.width(1)) register_2 (.D(I1), .en(LOAD), .clk(CLOCK), .Q(L1), .clr(RESET));
  Register #(.width(1)) register_3 (.D(I2), .en(LOAD), .clk(CLOCK), .Q(L2), .clr(RESET));
  Register #(.width(1)) register_4 (.D(I3), .en(LOAD), .clk(CLOCK), .Q(L3), .clr(RESET));
  Register #(.width(1)) register_5 (.D(I4), .en(LOAD), .clk(CLOCK), .Q(L4), .clr(RESET));
  Register #(.width(1)) register_6 (.D(I5), .en(LOAD), .clk(CLOCK), .Q(L5), .clr(RESET));
  Register #(.width(1)) register_7 (.D(I6), .en(LOAD), .clk(CLOCK), .Q(L6), .clr(RESET));
  Register #(.width(1)) register_8 (.D(I7), .en(LOAD), .clk(CLOCK), .Q(L7), .clr(RESET));
  assign O6 = ENABLE ? L6 : 1'bz;  // Controlled_Buffer controlled_buffer_1
  assign O7 = ENABLE ? L7 : 1'bz;  // Controlled_Buffer controlled_buffer_2
  assign O2 = ENABLE ? L2 : 1'bz;  // Controlled_Buffer controlled_buffer_3
  assign O3 = ENABLE ? L3 : 1'bz;  // Controlled_Buffer controlled_buffer_4
  assign O4 = ENABLE ? L4 : 1'bz;  // Controlled_Buffer controlled_buffer_5
  assign O5 = ENABLE ? L5 : 1'bz;  // Controlled_Buffer controlled_buffer_6
  assign O0 = ENABLE ? L0 : 1'bz;  // Controlled_Buffer controlled_buffer_7
  assign O1 = ENABLE ? L1 : 1'bz;  // Controlled_Buffer controlled_buffer_8
endmodule

module ALU (
  input  ENABLE,
  input  su,
  input  A7,
  input  A6,
  input  A5,
  input  A4,
  input  A3,
  input  A2,
  input  A1,
  input  A0,
  input  B7,
  input  B6,
  input  B5,
  input  B4,
  input  B3,
  input  B2,
  input  B1,
  input  B0,
  output L7,
  output L6,
  output L5,
  output L4,
  output L3,
  output L2,
  output L1,
  output L0,
  output E0,
  output CF,
  output ZF,
  output E1,
  output E2,
  output E3,
  output E4,
  output E5,
  output E6,
  output E7
);

  wire [7:0] xor_8_out;

  xor xor_1 (xor_8_out[7], B7, su);
  xor xor_2 (xor_8_out[6], B6, su);
  xor xor_3 (xor_8_out[5], B5, su);
  Adder adder_1 (
    .a({A7, A6, A5, A4, A3, A2, A1, A0}), .b(xor_8_out), .out({L7, L6, L5, L4, L3, L2, L1, L0}), .cin(su),
    .cout(CF));
  xor xor_4 (xor_8_out[4], B4, su);
  xor xor_5 (xor_8_out[3], B3, su);
  xor xor_6 (xor_8_out[2], B2, su);
  xor xor_7 (xor_8_out[1], B1, su);
  xor xor_8 (xor_8_out[0], B0, su);
  nor nor_1 (ZF, L0, L1, L2, L3, L4, L5, L6, L7);
  assign E0 = ENABLE ? L0 : 1'bz;  // Controlled_Buffer controlled_buffer_1
  assign E1 = ENABLE ? L1 : 1'bz;  // Controlled_Buffer controlled_buffer_2
  assign E2 = ENABLE ? L2 : 1'bz;  // Controlled_Buffer controlled_buffer_3
  assign E3 = ENABLE ? L3 : 1'bz;  // Controlled_Buffer controlled_buffer_4
  assign E4 = ENABLE ? L4 : 1'bz;  // Controlled_Buffer controlled_buffer_5
  assign E5 = ENABLE ? L5 : 1'bz;  // Controlled_Buffer controlled_buffer_6
  assign E6 = ENABLE ? L6 : 1'bz;  // Controlled_Buffer controlled_buffer_7
  assign E7 = ENABLE ? L7 : 1'bz;  // Controlled_Buffer controlled_buffer_8
endmodule

module registro_8bits_B (
  input  CLOCK,
  input  LOAD,
  input  RESET,
  input  ENABLE,
  input  I0,
  input  I1,
  input  I2,
  input  I3,
  input  I4,
  input  I5,
  input  I6,
  input  I7,
  output L0,
  output L1,
  output L2,
  output L3,
  output L4,
  output L5,
  output L6,
  output L7,
  output O0,
  output O1,
  output O2,
  output O3,
  output O4,
  output O5,
  output O6,
  output O7
);

  Register #(.width(1)) register_1 (.D(I0), .en(LOAD), .clk(CLOCK), .Q(L0), .clr(RESET));
  Register #(.width(1)) register_2 (.D(I1), .en(LOAD), .clk(CLOCK), .Q(L1), .clr(RESET));
  Register #(.width(1)) register_3 (.D(I2), .en(LOAD), .clk(CLOCK), .Q(L2), .clr(RESET));
  Register #(.width(1)) register_4 (.D(I3), .en(LOAD), .clk(CLOCK), .Q(L3), .clr(RESET));
  Register #(.width(1)) register_5 (.D(I4), .en(LOAD), .clk(CLOCK), .Q(L4), .clr(RESET));
  Register #(.width(1)) register_6 (.D(I5), .en(LOAD), .clk(CLOCK), .Q(L5), .clr(RESET));
  Register #(.width(1)) register_7 (.D(I6), .en(LOAD), .clk(CLOCK), .Q(L6), .clr(RESET));
  Register #(.width(1)) register_8 (.D(I7), .en(LOAD), .clk(CLOCK), .Q(L7), .clr(RESET));
  assign O6 = ENABLE ? L6 : 1'bz;  // Controlled_Buffer controlled_buffer_1
  assign O7 = ENABLE ? L7 : 1'bz;  // Controlled_Buffer controlled_buffer_2
  assign O2 = ENABLE ? L2 : 1'bz;  // Controlled_Buffer controlled_buffer_3
  assign O3 = ENABLE ? L3 : 1'bz;  // Controlled_Buffer controlled_buffer_4
  assign O4 = ENABLE ? L4 : 1'bz;  // Controlled_Buffer controlled_buffer_5
  assign O5 = ENABLE ? L5 : 1'bz;  // Controlled_Buffer controlled_buffer_6
  assign O0 = ENABLE ? L0 : 1'bz;  // Controlled_Buffer controlled_buffer_7
  assign O1 = ENABLE ? L1 : 1'bz;  // Controlled_Buffer controlled_buffer_8
endmodule

module MAR (
  input  CLOCK,
  input  LOAD,
  input  RESET,
  input  ENABLE,
  input  I0,
  input  I1,
  input  I2,
  input  I3,
  input  I4,
  input  I5,
  input  I6,
  input  I7,
  output L0,
  output L1,
  output L2,
  output L3,
  output L4,
  output L5,
  output L6,
  output L7,
  output L8,
  output L9,
  output LA,
  output LB,
  output LC,
  output LD,
  output LE,
  output LF,
  output [15:0] ADDRS
);

  wire register_1_q, register_2_q, register_3_q, register_4_q, register_5_q, register_6_q, register_7_q,
       register_8_q;

  Register #(.width(1)) register_1 (.D(I0), .en(LOAD), .clk(CLOCK), .Q(register_1_q), .clr(RESET));
  Register #(.width(1)) register_2 (.D(I1), .en(LOAD), .clk(CLOCK), .Q(register_2_q), .clr(RESET));
  Register #(.width(1)) register_3 (.D(I2), .en(LOAD), .clk(CLOCK), .Q(register_3_q), .clr(RESET));
  Register #(.width(1)) register_4 (.D(I3), .en(LOAD), .clk(CLOCK), .Q(register_4_q), .clr(RESET));
  Register #(.width(1)) register_5 (.D(I4), .en(LOAD), .clk(CLOCK), .Q(register_5_q), .clr(RESET));
  Register #(.width(1)) register_6 (.D(I5), .en(LOAD), .clk(CLOCK), .Q(register_6_q), .clr(RESET));
  Register #(.width(1)) register_7 (.D(I6), .en(LOAD), .clk(CLOCK), .Q(register_7_q), .clr(RESET));
  Register #(.width(1)) register_8 (.D(I7), .en(LOAD), .clk(CLOCK), .Q(register_8_q), .clr(RESET));
  decoder_4bits decoder_4bits_1 (
    .I3(register_4_q), .I2(register_3_q), .I1(register_2_q), .I0(register_1_q), .ENABLE(1'b1), .DF(LF),
    .DE(LE), .DD(LD), .DC(LC), .DB(LB), .DA(LA), .D9(L9), .D8(L8), .D7(L7), .D6(L6), .D5(L5), .D4(L4),
    .D3(L3), .D2(L2), .D1(L1), .D0(L0));
  assign ADDRS[4] = ENABLE ? L4 : 1'bz;  // Controlled_Buffer controlled_buffer_1
  assign ADDRS[5] = ENABLE ? L5 : 1'bz;  // Controlled_Buffer controlled_buffer_2
  assign ADDRS[6] = ENABLE ? L6 : 1'bz;  // Controlled_Buffer controlled_buffer_3
  assign ADDRS[7] = ENABLE ? L7 : 1'bz;  // Controlled_Buffer controlled_buffer_4
  assign ADDRS[12] = ENABLE ? LC : 1'bz;  // Controlled_Buffer controlled_buffer_5
  assign ADDRS[13] = ENABLE ? LD : 1'bz;  // Controlled_Buffer controlled_buffer_6
  assign ADDRS[14] = ENABLE ? LE : 1'bz;  // Controlled_Buffer controlled_buffer_7
  assign ADDRS[15] = ENABLE ? LF : 1'bz;  // Controlled_Buffer controlled_buffer_8
  assign ADDRS[0] = ENABLE ? L0 : 1'bz;  // Controlled_Buffer controlled_buffer_9
  assign ADDRS[1] = ENABLE ? L1 : 1'bz;  // Controlled_Buffer controlled_buffer_10
  assign ADDRS[2] = ENABLE ? L2 : 1'bz;  // Controlled_Buffer controlled_buffer_11
  assign ADDRS[3] = ENABLE ? L3 : 1'bz;  // Controlled_Buffer controlled_buffer_12
  assign ADDRS[8] = ENABLE ? L8 : 1'bz;  // Controlled_Buffer controlled_buffer_13
  assign ADDRS[9] = ENABLE ? L9 : 1'bz;  // Controlled_Buffer controlled_buffer_14
  assign ADDRS[10] = ENABLE ? LA : 1'bz;  // Controlled_Buffer controlled_buffer_15
  assign ADDRS[11] = ENABLE ? LB : 1'bz;  // Controlled_Buffer controlled_buffer_16
endmodule

module PROGRAM_COUNTER (
  input  COut,
  input  CEnable,
  input  CWrite,
  input  CReset,
  input  CLOCK,
  input  I7,
  input  I6,
  input  I5,
  input  I4,
  input  I3,
  input  I2,
  input  I1,
  input  I0,
  output O7,
  output O6,
  output O5,
  output O4,
  output O3,
  output O2,
  output O1,
  output O0,
  output L7,
  output L6,
  output L5,
  output L4,
  output L3,
  output L2,
  output L1,
  output L0
);

  wire and_1_out, and_2_out, and_3_out, and_4_out, and_5_out, and_6_out, and_7_out, and_8_out, and_9_out,
       and_10_out, and_11_out, and_12_out, and_13_out, and_14_out, and_15_out, and_16_out, j_k_ff_2_qn,
       j_k_ff_3_qn, j_k_ff_4_qn, j_k_ff_5_qn, j_k_ff_6_qn, j_k_ff_7_qn, j_k_ff_8_qn, or_1_out, or_2_out,
       or_3_out, or_4_out, or_5_out, or_6_out, or_7_out, or_8_out;

  J_K_Flip_Flop j_k_ff_1 (
    .J(CEnable), .K(CEnable), .clk(j_k_ff_2_qn), .Q(L7), .preset(and_1_out), .reset(or_1_out));  // open: Qn
  or or_1 (or_1_out, CReset, and_2_out);
  and and_1 (and_1_out, CWrite, I7, CLOCK);
  and and_2 (and_2_out, CWrite, ~I7, CLOCK);  // AND_Gate
  J_K_Flip_Flop j_k_ff_2 (
    .J(CEnable), .K(CEnable), .clk(j_k_ff_3_qn), .Q(L6), .Qn(j_k_ff_2_qn), .preset(and_3_out),
    .reset(or_2_out));
  or or_2 (or_2_out, CReset, and_4_out);
  and and_3 (and_3_out, CWrite, I6, CLOCK);
  and and_4 (and_4_out, CWrite, ~I6, CLOCK);  // AND_Gate
  assign O7 = COut ? L7 : 1'bz;  // Controlled_Buffer controlled_buffer_1
  assign O6 = COut ? L6 : 1'bz;  // Controlled_Buffer controlled_buffer_2
  J_K_Flip_Flop j_k_ff_3 (
    .J(CEnable), .K(CEnable), .clk(j_k_ff_4_qn), .Q(L5), .Qn(j_k_ff_3_qn), .preset(and_5_out),
    .reset(or_3_out));
  or or_3 (or_3_out, CReset, and_6_out);
  and and_5 (and_5_out, CWrite, I5, CLOCK);
  and and_6 (and_6_out, CWrite, ~I5, CLOCK);  // AND_Gate
  assign O5 = COut ? L5 : 1'bz;  // Controlled_Buffer controlled_buffer_3
  assign O4 = COut ? L4 : 1'bz;  // Controlled_Buffer controlled_buffer_4
  assign O3 = COut ? L3 : 1'bz;  // Controlled_Buffer controlled_buffer_5
  assign O2 = COut ? L2 : 1'bz;  // Controlled_Buffer controlled_buffer_6
  J_K_Flip_Flop j_k_ff_4 (
    .J(CEnable), .K(CEnable), .clk(j_k_ff_5_qn), .Q(L4), .Qn(j_k_ff_4_qn), .preset(and_7_out),
    .reset(or_4_out));
  or or_4 (or_4_out, CReset, and_8_out);
  and and_7 (and_7_out, CWrite, I4, CLOCK);
  and and_8 (and_8_out, CWrite, ~I4, CLOCK);  // AND_Gate
  assign O1 = COut ? L1 : 1'bz;  // Controlled_Buffer controlled_buffer_7
  assign O0 = COut ? L0 : 1'bz;  // Controlled_Buffer controlled_buffer_8
  J_K_Flip_Flop j_k_ff_5 (
    .J(CEnable), .K(CEnable), .clk(j_k_ff_6_qn), .Q(L3), .Qn(j_k_ff_5_qn), .preset(and_9_out),
    .reset(or_5_out));
  or or_5 (or_5_out, CReset, and_10_out);
  and and_9 (and_9_out, CWrite, I3, CLOCK);
  J_K_Flip_Flop j_k_ff_6 (
    .J(CEnable), .K(CEnable), .clk(j_k_ff_7_qn), .Q(L2), .Qn(j_k_ff_6_qn), .preset(and_11_out),
    .reset(or_6_out));
  and and_10 (and_10_out, CWrite, ~I3, CLOCK);  // AND_Gate
  and and_11 (and_11_out, CWrite, I2, CLOCK);
  J_K_Flip_Flop j_k_ff_7 (
    .J(CEnable), .K(CEnable), .clk(j_k_ff_8_qn), .Q(L1), .Qn(j_k_ff_7_qn), .preset(and_13_out),
    .reset(or_7_out));
  or or_6 (or_6_out, CReset, and_12_out);
  and and_12 (and_12_out, CWrite, ~I2, CLOCK);  // AND_Gate
  and and_13 (and_13_out, CWrite, I1, CLOCK);
  or or_7 (or_7_out, CReset, and_15_out);
  and and_14 (and_14_out, CWrite, I0, CLOCK);
  and and_15 (and_15_out, CWrite, ~I1, CLOCK);  // AND_Gate
  J_K_Flip_Flop j_k_ff_8 (
    .J(CEnable), .K(CEnable), .clk(CLOCK), .Q(L0), .Qn(j_k_ff_8_qn), .preset(and_14_out), .reset(or_8_out));
  or or_8 (or_8_out, CReset, and_16_out);
  and and_16 (and_16_out, CWrite, ~I0, CLOCK);  // AND_Gate
endmodule

module flags_rgister (
  input  CLOCK,
  input  LOAD,
  input  RESET,
  input  ENABLE,
  input  I0,
  input  I1,
  output L0,
  output L1,
  output O0,
  output O1
);

  Register #(.width(1)) register_1 (.D(I0), .en(LOAD), .clk(CLOCK), .Q(L0), .clr(RESET));
  Register #(.width(1)) register_2 (.D(I1), .en(LOAD), .clk(CLOCK), .Q(L1), .clr(RESET));
  assign O0 = ENABLE ? L0 : 1'bz;  // Controlled_Buffer controlled_buffer_1
  assign O1 = ENABLE ? L1 : 1'bz;  // Controlled_Buffer controlled_buffer_2
endmodule

module decoder_4bits (
  input  ENABLE,
  input  I3,
  input  I2,
  input  I1,
  input  I0,
  output DF,
  output DE,
  output DD,
  output DC,
  output DB,
  output DA,
  output D9,
  output D8,
  output D7,
  output D6,
  output D5,
  output D4,
  output D3,
  output D2,
  output D1,
  output D0
);

  wire and_1_out, and_2_out, and_3_out, and_4_out, and_5_out, and_6_out, and_7_out, and_8_out, and_9_out,
       and_10_out, and_11_out, and_12_out, and_13_out, and_14_out, and_15_out, and_16_out, not_1_out,
       not_2_out, not_3_out, not_4_out;

  not not_1 (not_1_out, I3);
  not not_2 (not_2_out, I2);
  not not_3 (not_3_out, I1);
  not not_4 (not_4_out, I0);
  and and_1 (and_1_out, not_1_out, not_2_out, not_3_out, not_4_out);
  and and_2 (and_2_out, not_1_out, not_2_out, not_3_out, I0);
  and and_3 (and_3_out, not_1_out, not_2_out, I1, not_4_out);
  and and_4 (and_4_out, not_1_out, not_2_out, I1, I0);
  and and_5 (and_5_out, not_1_out, I2, not_3_out, not_4_out);
  and and_6 (and_6_out, not_1_out, I2, not_3_out, I0);
  and and_7 (and_7_out, not_1_out, I2, I1, not_4_out);
  and and_8 (and_8_out, not_1_out, I2, I1, I0);
  and and_9 (and_9_out, I3, not_2_out, not_3_out, not_4_out);
  and and_10 (and_10_out, I3, not_2_out, not_3_out, I0);
  and and_11 (and_11_out, I3, not_2_out, I1, not_4_out);
  and and_12 (and_12_out, I3, not_2_out, I1, I0);
  and and_13 (and_13_out, I3, I2, not_3_out, not_4_out);
  and and_14 (and_14_out, I3, I2, not_3_out, I0);
  and and_15 (and_15_out, I3, I2, I1, not_4_out);
  and and_16 (and_16_out, I3, I2, I1, I0);
  assign DF = ENABLE ? and_16_out : 1'bz;  // Controlled_Buffer controlled_buffer_1
  assign DE = ENABLE ? and_15_out : 1'bz;  // Controlled_Buffer controlled_buffer_2
  assign DD = ENABLE ? and_14_out : 1'bz;  // Controlled_Buffer controlled_buffer_3
  assign DC = ENABLE ? and_13_out : 1'bz;  // Controlled_Buffer controlled_buffer_4
  assign DB = ENABLE ? and_12_out : 1'bz;  // Controlled_Buffer controlled_buffer_5
  assign DA = ENABLE ? and_11_out : 1'bz;  // Controlled_Buffer controlled_buffer_6
  assign D9 = ENABLE ? and_10_out : 1'bz;  // Controlled_Buffer controlled_buffer_7
  assign D8 = ENABLE ? and_9_out : 1'bz;  // Controlled_Buffer controlled_buffer_8
  assign D7 = ENABLE ? and_8_out : 1'bz;  // Controlled_Buffer controlled_buffer_9
  assign D6 = ENABLE ? and_7_out : 1'bz;  // Controlled_Buffer controlled_buffer_10
  assign D5 = ENABLE ? and_6_out : 1'bz;  // Controlled_Buffer controlled_buffer_11
  assign D4 = ENABLE ? and_5_out : 1'bz;  // Controlled_Buffer controlled_buffer_12
  assign D3 = ENABLE ? and_4_out : 1'bz;  // Controlled_Buffer controlled_buffer_13
  assign D2 = ENABLE ? and_3_out : 1'bz;  // Controlled_Buffer controlled_buffer_14
  assign D1 = ENABLE ? and_2_out : 1'bz;  // Controlled_Buffer controlled_buffer_15
  assign D0 = ENABLE ? and_1_out : 1'bz;  // Controlled_Buffer controlled_buffer_16
endmodule

module INSTRUCCION_REGISTER (
  input  CLOCK,
  input  LOAD,
  input  RESET,
  input  ENABLE,
  input  I0,
  input  I1,
  input  I2,
  input  I3,
  input  I4,
  input  I5,
  input  I6,
  input  I7,
  output L0,
  output L1,
  output L2,
  output L3,
  output L4,
  output L5,
  output L6,
  output L7,
  output O0,
  output O1,
  output O2,
  output O3,
  output O4,
  output O5,
  output O6,
  output O7
);

  Register #(.width(1)) register_1 (.D(I0), .en(LOAD), .clk(CLOCK), .Q(L0), .clr(RESET));
  Register #(.width(1)) register_2 (.D(I1), .en(LOAD), .clk(CLOCK), .Q(L1), .clr(RESET));
  Register #(.width(1)) register_3 (.D(I2), .en(LOAD), .clk(CLOCK), .Q(L2), .clr(RESET));
  Register #(.width(1)) register_4 (.D(I3), .en(LOAD), .clk(CLOCK), .Q(L3), .clr(RESET));
  Register #(.width(1)) register_5 (.D(I4), .en(LOAD), .clk(CLOCK), .Q(L4), .clr(RESET));
  Register #(.width(1)) register_6 (.D(I5), .en(LOAD), .clk(CLOCK), .Q(L5), .clr(RESET));
  Register #(.width(1)) register_7 (.D(I6), .en(LOAD), .clk(CLOCK), .Q(L6), .clr(RESET));
  Register #(.width(1)) register_8 (.D(I7), .en(LOAD), .clk(CLOCK), .Q(L7), .clr(RESET));
  assign O6 = ENABLE ? L6 : 1'bz;  // Controlled_Buffer controlled_buffer_1
  assign O7 = ENABLE ? L7 : 1'bz;  // Controlled_Buffer controlled_buffer_2
  assign O2 = ENABLE ? L2 : 1'bz;  // Controlled_Buffer controlled_buffer_3
  assign O3 = ENABLE ? L3 : 1'bz;  // Controlled_Buffer controlled_buffer_4
  assign O4 = ENABLE ? L4 : 1'bz;  // Controlled_Buffer controlled_buffer_5
  assign O5 = ENABLE ? L5 : 1'bz;  // Controlled_Buffer controlled_buffer_6
  assign O0 = ENABLE ? L0 : 1'bz;  // Controlled_Buffer controlled_buffer_7
  assign O1 = ENABLE ? L1 : 1'bz;  // Controlled_Buffer controlled_buffer_8
endmodule
